// Logisim project s-mips.circ as structural Verilog
module S_MIPS_Board (
  input  DESHABILITAR_DISPATCHER,
  output halt
);

  wire button_1_out, CLK, CS, d_ff_1_q, LCLR, LoadRAM, LoadRAMOn, LW, R_R_W, R_W, ram_dispatcher_1_finished,
       RCS, Reset_out, RST, TTY_EN;
  wire [2:0] KDB;
  wire [3:0] LMask, Mask, ram_1_read_time, ram_1_write_time, RMask;
  wire [6:0] KDB_DATA, TTY_DATA;
  wire [15:0] Addr, LAddr, RAddr;
  wire [31:0] I0, I1, I2, I3, LData, ram_1_data_out_0, ram_1_data_out_1, ram_1_data_out_2, ram_1_data_out_3,
       RI0, RI1, RI2, RI3;

  TTY #(.rows(25), .cols(80)) tty_1 (.data(TTY_DATA), .clk(CLK), .we(TTY_EN), .clr(RST));
  not not_1 (LoadRAMOn, ram_dispatcher_1_finished);
  RAM_Dispatcher ram_dispatcher_1 (
    .WriteTime(ram_1_write_time), .Clock(CLK), .Data(LData), .Address(LAddr), .Mask(LMask),
    .Finished(ram_dispatcher_1_finished), .Write(LW), .CLR(LCLR));
  Keyboard #(.buflen(64)) keyboard_1 (.clk(CLK), .re(KDB[0]), .avail(KDB[2]), .data(KDB_DATA));  // open: clr
  RAM ram_1 (
    .Address(RAddr), .Data_Out_0(ram_1_data_out_0), .Data_Out_1(ram_1_data_out_1),
    .Data_Out_2(ram_1_data_out_2), .Data_Out_3(ram_1_data_out_3), .Data_In_0(RI0), .Data_In_1(RI1),
    .Data_In_2(RI2), .Data_In_3(RI3), .Mask(RMask), .nRead_Write(R_R_W), .Chip_Select(RCS),
    .Read_Time(ram_1_read_time), .Reset(button_1_out), .Write_Time(ram_1_write_time));
  Button button_1 (.out(button_1_out));
  D_Flip_Flop d_ff_1 (.clk(CLK), .D(1'b1), .Q(d_ff_1_q), .reset(Reset_out));  // open: Qn, preset, en
  Button Reset (.out(Reset_out));
  S_MIPS s_mips_1 ();
  D_Flip_Flop d_ff_2 (.clk(CLK), .D(d_ff_1_q), .Qn(LCLR), .reset(Reset_out));  // open: Q, preset, en
  or or_1 (RST, LCLR, LoadRAM);
  Clock clock_1 (.out(CLK));
  Multiplexer #(.width(32), .enable("false")) multiplexer_1 (.in0(I0), .in1(LData), .out(RI0), .sel(LoadRAM));
  Multiplexer #(.width(32), .enable("false")) multiplexer_2 (.in0(I1), .in1(LData), .out(RI1), .sel(LoadRAM));
  Multiplexer #(.width(32), .enable("false")) multiplexer_3 (.in0(I2), .in1(LData), .out(RI2), .sel(LoadRAM));
  Multiplexer #(.width(32), .enable("false")) multiplexer_4 (.in0(I3), .in1(LData), .out(RI3), .sel(LoadRAM));
  and and_1 (LoadRAM, ~DESHABILITAR_DISPATCHER, LoadRAMOn);  // AND_Gate
  Multiplexer #(.width(16), .enable("false")) multiplexer_5 (.in0(Addr), .in1(LAddr), .out(RAddr), .sel(LoadRAM));
  Multiplexer #(.width(4), .enable("false")) multiplexer_6 (.in0(Mask), .in1(LMask), .out(RMask), .sel(LoadRAM));
  Multiplexer #(.enable("false")) multiplexer_7 (.in0(CS), .in1(LW), .out(RCS), .sel(LoadRAM));
  Multiplexer #(.enable("false")) multiplexer_8 (.in0(R_W), .in1(LW), .out(R_R_W), .sel(LoadRAM));

  // Notes on the sheet:
  //   NO MODIFICAR
  //   Keyboard
endmodule

module RAM (
  input  [15:0] Address,
  input  [31:0] Data_In_0,
  input  [31:0] Data_In_1,
  input  [31:0] Data_In_2,
  input  [31:0] Data_In_3,
  input  [3:0] Mask,
  input  nRead_Write,
  input  Chip_Select,
  input  Reset,
  output [31:0] Data_Out_0,
  output [31:0] Data_Out_1,
  output [31:0] Data_Out_2,
  output [31:0] Data_Out_3,
  output [3:0] Read_Time,
  output [3:0] Write_Time
);

  wire and_2_out, and_3_out, and_4_out, and_5_out, and_6_out, and_7_out, and_8_out, and_9_out, Changed, CLK,
       comparator_2_eq, comparator_3_eq, comparator_4_eq, comparator_5_eq, comparator_6_eq, Count,
       demultiplexer_3_out0, Idle, Idle_q, Load, Load0, Load1, nand_1_out, or_1_out, or_2_out, or_3_out,
       or_4_out, or_5_out, or_6_out, or_7_out, or_8_out, or_9_out, or_10_out, Proc_q, Update_Mem, Zero_Time;
  wire [3:0] counter_1_q, multiplexer_1_out, subtractor_1_out;
  wire [31:0] register_1_q, register_2_q, register_3_q, register_4_q, register_5_q;

  // Probe on 4'b0011
  // Probe on 4'b0010
  Multiplexer #(.width(4), .enable("false")) multiplexer_1 (
    .in0(4'b0011), .in1(4'b0010), .out(multiplexer_1_out), .sel(nRead_Write));
  or or_1 (or_1_out, Idle, Update_Mem);
  or or_2 (or_2_out, ~Chip_Select, Reset);  // OR_Gate
  Subtractor #(.width(4)) subtractor_1 (.a(multiplexer_1_out), .b(4'b0010), .out(subtractor_1_out));  // open: bin, bout
  Demultiplexer #(.enable("false")) demultiplexer_1 (.out0(Idle), .out1(Load0), .in(Idle_q), .sel(Changed));
  D_Flip_Flop u_Idle (.clk(CLK), .D(or_1_out), .Q(Idle_q), .preset(or_2_out));  // open: Qn, en, reset
  // Probe on counter_1_q
  Counter #(.width(4), .max('hf)) counter_1 (
    .load(Load), .D(subtractor_1_out), .count(Count), .Q(counter_1_q), .clk(CLK), .clr(or_3_out));  // open: carry
  or or_3 (or_3_out, ~Chip_Select, Reset);  // OR_Gate
  Comparator #(.width(4), .mode("unsigned")) comparator_1 (
    .a(4'b0000), .b(counter_1_q), .eq(Zero_Time));  // open: gt, lt
  or or_4 (or_4_out, Count, Load0, Load1);
  Register #(.width(32)) register_1 (.D(Data_In_0), .en(Chip_Select), .Q(register_1_q), .clk(CLK), .clr(or_5_out));
  or or_5 (or_5_out, ~Chip_Select, Reset);  // OR_Gate
  Register #(.width(32)) register_2 (.D(Data_In_1), .en(Chip_Select), .Q(register_2_q), .clk(CLK), .clr(or_6_out));
  or or_6 (or_6_out, ~Chip_Select, Reset);  // OR_Gate
  Register #(.width(32)) register_3 (.D(Data_In_2), .en(Chip_Select), .Q(register_3_q), .clk(CLK), .clr(or_7_out));
  or or_7 (or_7_out, ~Chip_Select, Reset);  // OR_Gate
  Register #(.width(32)) register_4 (.D(Data_In_3), .en(Chip_Select), .Q(register_4_q), .clk(CLK), .clr(or_8_out));
  or or_8 (or_8_out, ~Chip_Select, Reset);  // OR_Gate
  Register #(.width(32)) register_5 (
    .D({{11{1'b1}}, nRead_Write, Mask, Address}), .en(Chip_Select), .Q(register_5_q), .clk(CLK),
    .clr(or_9_out));
  or or_9 (or_9_out, ~Chip_Select, Reset);  // OR_Gate
  D_Flip_Flop Proc (.clk(CLK), .D(or_4_out), .Q(Proc_q), .reset(or_10_out));  // open: Qn, preset, en
  or or_10 (or_10_out, ~Chip_Select, Reset);  // OR_Gate
  Demultiplexer #(.enable("false")) demultiplexer_2 (
    .out0(Count), .out1(Update_Mem), .in(demultiplexer_3_out0), .sel(Zero_Time));
  Demultiplexer #(.enable("false")) demultiplexer_3 (
    .out0(demultiplexer_3_out0), .out1(Load1), .in(Proc_q), .sel(Changed));
  Clock clock_1 (.out(CLK));
  Comparator #(.width(32)) comparator_2 (.a(register_1_q), .b(Data_In_0), .eq(comparator_2_eq));  // open: gt, lt
  Comparator #(.width(32)) comparator_3 (.a(register_2_q), .b(Data_In_1), .eq(comparator_3_eq));  // open: gt, lt
  Comparator #(.width(32)) comparator_4 (.a(register_3_q), .b(Data_In_2), .eq(comparator_4_eq));  // open: gt, lt
  Comparator #(.width(32)) comparator_5 (.a(register_4_q), .b(Data_In_3), .eq(comparator_5_eq));  // open: gt, lt
  Comparator #(.width(32)) comparator_6 (
    .a(register_5_q), .b({{11{1'b1}}, nRead_Write, Mask, Address}), .eq(comparator_6_eq));  // open: gt, lt
  nand nand_1 (nand_1_out, comparator_6_eq, comparator_2_eq, comparator_3_eq, comparator_4_eq, comparator_5_eq);
  and and_1 (Changed, nand_1_out, Chip_Select);
  or or_11 (Load, Count, Load1, Load0);
  and and_2 (and_2_out, Mask[0], Update_Mem, nRead_Write);
  and and_3 (and_3_out, Mask[1], Update_Mem, nRead_Write);
  and and_4 (and_4_out, Mask[2], Update_Mem, nRead_Write);
  and and_5 (and_5_out, Mask[3], Update_Mem, nRead_Write);
  RAM_part #(.addrWidth(16), .dataWidth(32), .bus("separate")) ram_1 (
    .addr(Address), .din(Data_In_0), .data(Data_Out_0), .str(and_2_out), .sel(Chip_Select), .clk(CLK),
    .ld(and_6_out), .clr(Reset));
  and and_6 (and_6_out, ~nRead_Write, Idle);  // AND_Gate
  RAM_part #(.addrWidth(16), .dataWidth(32), .bus("separate")) ram_2 (
    .addr(Address), .din(Data_In_1), .data(Data_Out_1), .str(and_3_out), .sel(Chip_Select), .clk(CLK),
    .ld(and_7_out), .clr(Reset));
  and and_7 (and_7_out, ~nRead_Write, Idle);  // AND_Gate
  RAM_part #(.addrWidth(16), .dataWidth(32), .bus("separate")) ram_3 (
    .addr(Address), .din(Data_In_2), .data(Data_Out_2), .str(and_4_out), .sel(Chip_Select), .clk(CLK),
    .ld(and_8_out), .clr(Reset));
  and and_8 (and_8_out, ~nRead_Write, Idle);  // AND_Gate
  RAM_part #(.addrWidth(16), .dataWidth(32), .bus("separate")) ram_4 (
    .addr(Address), .din(Data_In_3), .data(Data_Out_3), .str(and_5_out), .sel(Chip_Select), .clk(CLK),
    .ld(and_9_out), .clr(Reset));
  and and_9 (and_9_out, ~nRead_Write, Idle);  // AND_Gate

  assign Read_Time = 4'b0011;
  assign Write_Time = 4'b0010;

  // Other names for the same wires on the sheet: M0 = Mask[0]; M1 = Mask[1]; M2 = Mask[2]; M3 = Mask[3];
  //   RW = nRead_Write; CLR = Reset; CS = Chip_Select; Load2 = Count

  // Notes on the sheet:
  //   NO MODIFICAR
  //   excepto quizás los valores RT y WT
  //   BANK0
  //   BANK1
  //   BANK2
  //   BANK3
endmodule

module RAM_Dispatcher (
  input  [3:0] WriteTime,
  input  Clock,
  input  CLR,
  output [31:0] Data,
  output [15:0] Address,
  output [3:0] Mask,
  output Finished,
  output Write
);

  wire demultiplexer_2_out1, demultiplexer_3_out1, End, IDLE_q, IncAddr, Load, or_1_out, or_2_out, While_q,
       WriteEnd;
  wire [3:0] counter_1_q;
  wire [31:0] CurrentAddress_q;

  Counter #(.width(32), .max('hffffffff)) CurrentAddress (
    .count(IncAddr), .Q({CurrentAddress_q[31:18], Address, CurrentAddress_q[1:0]}), .clk(Clock), .clr(CLR));  // open: load, D, carry
  or or_1 (or_1_out, IncAddr, demultiplexer_3_out1, Finished);
  D_Flip_Flop IDLE (.clk(Clock), .D(or_1_out), .Q(IDLE_q), .preset(CLR));  // open: Qn, en, reset
  Demultiplexer #(.enable("false")) demultiplexer_1 (.out0(Load), .out1(Finished), .in(IDLE_q), .sel(End));
  D_Flip_Flop While (.clk(Clock), .D(or_2_out), .Q(While_q), .reset(CLR));  // open: Qn, preset, en
  or or_2 (or_2_out, Write, Load);
  RAM_part #(.addrWidth(18), .dataWidth(32)) ram_1 (
    .addr({Address, CurrentAddress_q[1:0]}), .data(Data), .clk(Clock));  // open: sel, ld, clr
  Demultiplexer #(.enable("false")) demultiplexer_2 (
    .out0(Write), .out1(demultiplexer_2_out1), .in(While_q), .sel(WriteEnd));
  Decoder #(.select(2)) decoder_1 (
    .out0(Mask[0]), .out1(Mask[1]), .out2(Mask[2]), .out3(Mask[3]), .sel(CurrentAddress_q[1:0]));  // open: en
  Demultiplexer #(.enable("false")) demultiplexer_3 (
    .out0(IncAddr), .out1(demultiplexer_3_out1), .in(demultiplexer_2_out1), .sel(End));
  Counter #(.width(4), .max('hf)) counter_1 (
    .load(Load), .D(WriteTime), .count(Write), .Q(counter_1_q), .clk(Clock));  // open: carry, clr
  Comparator #(.width(32)) comparator_1 (.a(Data), .b({32{1'b1}}), .eq(End));  // open: gt, lt
  Comparator #(.width(4)) comparator_2 (.a(4'b0000), .b(counter_1_q), .eq(WriteEnd));  // open: gt, lt

  // Other names for the same wires on the sheet: CLK = Clock; Count = Write; WT[3:0] = WriteTime
endmodule

module CPU_2_0 (
  input  [15:0] Address,
  input  Kbd_Available,
  input  [6:0] Kbd_ASCII_Data,
  input  Reset,
  input  [31:0] RAM_In_0,
  input  [31:0] RAM_In_1,
  input  [31:0] RAM_In_2,
  input  [31:0] RAM_In_3,
  input  [3:0] Read_Time,
  input  [3:0] Write_Time,
  output Kbd_Enable,
  output Kbd_Clear,
  output [31:0] RAM_Out_0,
  output TTY_Enable,
  output [31:0] RAM_Out_1,
  output [6:0] TTY_ASCII_Data,
  output [31:0] RAM_Out_2,
  output Stop,
  output [31:0] RAM_Out_3,
  output [3:0] Mask,
  output nRead_Write,
  output Chip_Select
);

  wire Activation_Time_1, Activation_Time_2, Clock_1, Clock_2, instruction_decoder_1_clock_2,
       instruction_decoder_1_r___w, instruction_decoder_1_reset, Jmp;
  wire [3:0] counter_1_q, counter_2_q;
  wire [4:0] instruction_decoder_1_data_address, instruction_decoder_1_sa_2, instruction_decoder_1_sb_2;
  wire [15:0] instruction_decoder_1_constant;
  wire [31:0] ADDR, Inst, instruction_decoder_1_op_2, instruction_decoder_1_pc_2, PC, Pc_prime,
       Pc_prime_prime, Result;

  assign ADDR = {{16{1'b0}}, Address};  // Bit_Extender bit_extender_1
  Demultiplexer #(.select(2), .width(32)) demultiplexer_1 (
    .out0(RAM_Out_0), .out1(RAM_Out_1), .out2(RAM_Out_2), .out3(RAM_Out_3), .in(Result), .sel(PC[3:2]));  // open: en
  Multiplexer #(.select(2), .width(32)) multiplexer_1 (
    .in0(RAM_In_0), .in1(RAM_In_1), .in2(RAM_In_2), .in3(RAM_In_3), .out(Inst), .sel(PC[3:2]));  // open: en
  Counter #(.width(4), .max('hf)) counter_1 (.Q(counter_1_q), .clk(Clock_1));  // open: load, D, count, carry, clr
  Counter #(.width(4), .max('hf)) counter_2 (.Q(counter_2_q), .clk(Clock_2));  // open: load, D, count, carry, clr
  PC_3_0 pc_3_0_1 (
    .Clock_1(Activation_Time_1), .Clock_2(Activation_Time_2), .Rst(Reset), .ADDR(ADDR),
    .PC_prime_input(Pc_prime), .PC(PC), .PC_prime(Pc_prime_prime), .Jmp(Jmp));
  Clock u_clock_1 (.out(Clock_1));
  Clock u_clock_2 (.out(Clock_2));
  // Probe on counter_1_q
  Comparator #(.width(4)) comparator_1 (.a(counter_1_q), .b(Read_Time), .eq(Activation_Time_1));  // open: gt, lt
  // Probe on counter_2_q
  Comparator #(.width(4)) comparator_2 (.a(counter_2_q), .b(Write_Time), .eq(Activation_Time_2));  // open: gt, lt
  // Probe on PC
  // Probe on PC[3:2]
  Instruction_Decoder instruction_decoder_1 (
    .W_Id(nRead_Write), .Rst(Reset), .Instruction(Inst), .Clock(Clock_2), .Jmp(Jmp), .PC(PC),
    .Clock_2(instruction_decoder_1_clock_2), .R___W(instruction_decoder_1_r___w),
    .Data_Address(instruction_decoder_1_data_address), .Reset(instruction_decoder_1_reset),
    .Sa_2(instruction_decoder_1_sa_2), .Sb_2(instruction_decoder_1_sb_2),
    .Constant(instruction_decoder_1_constant), .Op_2(instruction_decoder_1_op_2),
    .PC_2(instruction_decoder_1_pc_2));  // open: Op, S_Mult, S_Div, SA, SB, DA, Mult, Div
  Data_Path data_path_1 (
    .Clock(instruction_decoder_1_clock_2), .RW(instruction_decoder_1_r___w),
    .DA(instruction_decoder_1_data_address), .Rst(instruction_decoder_1_reset),
    .SA(instruction_decoder_1_sa_2), .SB(instruction_decoder_1_sb_2), .Op(instruction_decoder_1_op_2),
    .Constant(instruction_decoder_1_constant), .Data_Output(Result), .Pc(instruction_decoder_1_pc_2),
    .Pc_prime(Pc_prime));  // open: A, B

  // Other names for the same wires on the sheet: CS = Chip_Select; KBD_AVAIL = Kbd_Available; KBD_CLR = Kbd_Clear;
  //   KBD_DATA[6:0] = Kbd_ASCII_Data; PC_value[1:0] = PC[3:2]; R1I[31:0] = RAM_In_0; R1O[31:0] = RAM_Out_0;
  //   R2I[31:0] = RAM_In_1; R2O[31:0] = RAM_Out_1; R3I[31:0] = RAM_In_2; R3O[31:0] = RAM_Out_2; R4I[31:0] = RAM_In_3;
  //   R4O[31:0] = RAM_Out_3; RAM_MASK[3:0] = Mask; Rst = Reset; TTY_DATA[6:0] = TTY_ASCII_Data; W_Id = nRead_Write

  // Notes on the sheet:
  //   RAM ADDRESS
  //   DATA FROM RAM
  //   DATA TO RAM
  //   DATA WRITE MASK
  //   RAM TIMING
  //   RAM CONTROL
  //   CU
  //   PC
  //   Timer Reader
  //   ID
  //   KEYBOARD
  //   TTY
  //   SEQUENCING
  //   Data Path
endmodule

// Mux
module MUX_32_32 (
  input  [31:0] Selector,
  input  [31:0] Data_Input_0,
  input  [31:0] Data_Input_1,
  input  [31:0] Data_Input_2,
  input  [31:0] Data_Input_3,
  input  [31:0] Data_Input_4,
  input  [31:0] Data_Input_5,
  input  [31:0] Data_Input_6,
  input  [31:0] Data_Input_7,
  input  [31:0] Data_Input_8,
  input  [31:0] Data_Input_9,
  input  [31:0] Data_Input_10,
  input  [31:0] Data_Input_11,
  input  [31:0] Data_Input_12,
  input  [31:0] Data_Input_13,
  input  [31:0] Data_Input_14,
  input  [31:0] Data_Input_15,
  input  [31:0] Data_Input_16,
  input  [31:0] Data_Input_17,
  input  [31:0] Data_Input_18,
  input  [31:0] Data_Input_19,
  input  [31:0] Data_Input_20,
  input  [31:0] Data_Input_21,
  input  [31:0] Data_Input_22,
  input  [31:0] Data_Input_23,
  input  [31:0] Data_Input_24,
  input  [31:0] Data_Input_25,
  input  [31:0] Data_Input_26,
  input  [31:0] Data_Input_27,
  input  [31:0] Data_Input_28,
  input  [31:0] Data_Input_29,
  input  [31:0] Data_Input_30,
  input  [31:0] Data_Input_31,
  output [31:0] Output
);

  wire not_1_out, not_2_out, not_3_out, not_4_out, not_5_out, not_6_out, not_7_out, not_8_out, not_9_out,
       not_10_out, not_11_out, not_12_out, not_13_out, not_14_out, not_15_out, not_16_out, not_17_out,
       not_18_out, not_19_out, not_20_out, not_21_out, not_22_out, not_23_out, not_24_out, not_25_out,
       not_26_out, not_27_out, not_28_out, not_29_out, not_30_out, not_31_out, not_32_out, not_33_out,
       not_35_out, not_36_out, not_37_out, not_38_out, not_39_out, not_40_out, not_41_out, not_42_out,
       not_43_out, not_44_out, not_45_out, not_46_out, not_47_out, not_48_out, not_49_out, not_50_out,
       not_51_out, not_52_out, not_53_out, not_54_out, not_55_out, not_56_out, not_57_out, not_58_out,
       not_59_out, not_60_out, not_61_out, not_62_out, not_63_out, not_64_out, not_65_out, not_66_out,
       not_68_out, not_69_out, not_70_out, not_71_out, not_72_out, not_73_out, not_74_out, not_75_out,
       not_76_out, not_77_out, not_78_out, not_79_out, not_80_out, not_81_out, not_82_out, not_83_out,
       not_84_out, not_85_out, not_86_out, not_87_out, not_88_out, not_89_out, not_90_out, not_91_out,
       not_92_out, not_93_out, not_94_out, not_95_out, not_96_out, not_97_out, not_98_out, not_99_out,
       not_101_out, not_102_out, not_103_out, not_104_out, not_105_out, not_106_out, not_107_out,
       not_108_out, not_109_out, not_110_out, not_111_out, not_112_out, not_113_out, not_114_out,
       not_115_out, not_116_out, not_117_out, not_118_out, not_119_out, not_120_out, not_121_out,
       not_122_out, not_123_out, not_124_out, not_125_out, not_126_out, not_127_out, not_128_out,
       not_129_out, not_130_out, not_131_out, not_132_out, not_134_out, not_135_out, not_136_out,
       not_137_out, not_138_out, not_139_out, not_140_out, not_141_out, not_142_out, not_143_out,
       not_144_out, not_145_out, not_146_out, not_147_out, not_148_out, not_149_out, not_150_out,
       not_151_out, not_152_out, not_153_out, not_154_out, not_155_out, not_156_out, not_157_out,
       not_158_out, not_159_out, not_160_out, not_161_out, not_162_out, not_163_out, not_164_out,
       not_166_out, not_167_out, not_168_out, not_169_out, not_170_out, not_171_out, not_172_out,
       not_173_out, not_174_out, not_175_out, not_176_out, not_177_out, not_178_out, not_179_out,
       not_180_out, not_181_out, not_182_out, not_183_out, not_184_out, not_185_out, not_186_out,
       not_187_out, not_188_out, not_189_out, not_190_out, not_191_out, not_192_out, not_193_out,
       not_194_out, not_195_out, not_196_out, not_197_out, not_198_out, not_200_out, not_201_out,
       not_202_out, not_203_out, not_204_out, not_205_out, not_206_out, not_207_out, not_208_out,
       not_209_out, not_210_out, not_211_out, not_212_out, not_213_out, not_214_out, not_215_out,
       not_216_out, not_217_out, not_218_out, not_219_out, not_220_out, not_221_out, not_222_out,
       not_223_out, not_224_out, not_225_out, not_226_out, not_227_out, not_228_out, not_229_out,
       not_230_out, not_231_out, not_233_out, not_234_out, not_235_out, not_236_out, not_237_out,
       not_238_out, not_239_out, not_240_out, not_241_out, not_242_out, not_243_out, not_244_out,
       not_245_out, not_246_out, not_247_out, not_248_out, not_249_out, not_250_out, not_251_out,
       not_252_out, not_253_out, not_254_out, not_255_out, not_256_out, not_257_out, not_258_out,
       not_259_out, not_260_out, not_261_out, not_262_out, not_263_out, not_264_out, not_266_out,
       not_267_out, not_268_out, not_269_out, not_270_out, not_271_out, not_272_out, not_273_out,
       not_274_out, not_275_out, not_276_out, not_277_out, not_278_out, not_279_out, not_280_out,
       not_281_out, not_282_out, not_283_out, not_284_out, not_285_out, not_286_out, not_287_out,
       not_288_out, not_289_out, not_290_out, not_291_out, not_292_out, not_293_out, not_294_out,
       not_295_out, not_296_out, not_297_out, not_299_out, not_300_out, not_301_out, not_302_out,
       not_303_out, not_304_out, not_305_out, not_306_out, not_307_out, not_308_out, not_309_out,
       not_310_out, not_311_out, not_312_out, not_313_out, not_314_out, not_315_out, not_316_out,
       not_317_out, not_318_out, not_319_out, not_320_out, not_321_out, not_322_out, not_323_out,
       not_324_out, not_325_out, not_326_out, not_327_out, not_328_out, not_329_out, not_330_out,
       not_332_out, not_333_out, not_334_out, not_335_out, not_336_out, not_337_out, not_338_out,
       not_339_out, not_340_out, not_341_out, not_342_out, not_343_out, not_344_out, not_345_out,
       not_346_out, not_347_out, not_348_out, not_349_out, not_350_out, not_351_out, not_352_out,
       not_353_out, not_354_out, not_355_out, not_356_out, not_357_out, not_358_out, not_359_out,
       not_360_out, not_361_out, not_362_out, not_363_out, not_365_out, not_366_out, not_367_out,
       not_368_out, not_369_out, not_370_out, not_371_out, not_372_out, not_373_out, not_374_out,
       not_375_out, not_376_out, not_377_out, not_378_out, not_379_out, not_380_out, not_381_out,
       not_382_out, not_383_out, not_384_out, not_385_out, not_386_out, not_387_out, not_388_out,
       not_389_out, not_390_out, not_391_out, not_392_out, not_393_out, not_394_out, not_395_out,
       not_396_out, not_398_out, not_399_out, not_400_out, not_401_out, not_402_out, not_403_out,
       not_404_out, not_405_out, not_406_out, not_407_out, not_408_out, not_409_out, not_410_out,
       not_411_out, not_412_out, not_413_out, not_414_out, not_415_out, not_416_out, not_417_out,
       not_418_out, not_419_out, not_420_out, not_421_out, not_422_out, not_423_out, not_424_out,
       not_425_out, not_426_out, not_427_out, not_428_out, not_429_out, not_431_out, not_432_out,
       not_433_out, not_434_out, not_435_out, not_436_out, not_437_out, not_438_out, not_439_out,
       not_440_out, not_441_out, not_442_out, not_443_out, not_444_out, not_445_out, not_446_out,
       not_447_out, not_448_out, not_449_out, not_450_out, not_451_out, not_452_out, not_453_out,
       not_454_out, not_455_out, not_456_out, not_457_out, not_458_out, not_459_out, not_460_out,
       not_461_out, not_462_out, not_464_out, not_465_out, not_466_out, not_467_out, not_468_out,
       not_469_out, not_470_out, not_471_out, not_472_out, not_473_out, not_474_out, not_475_out,
       not_476_out, not_477_out, not_478_out, not_479_out, not_480_out, not_481_out, not_482_out,
       not_483_out, not_484_out, not_485_out, not_486_out, not_487_out, not_488_out, not_489_out,
       not_490_out, not_491_out, not_492_out, not_493_out, not_494_out, not_495_out, not_497_out,
       not_498_out, not_499_out, not_500_out, not_501_out, not_502_out, not_503_out, not_504_out,
       not_505_out, not_506_out, not_507_out, not_508_out, not_509_out, not_510_out, not_511_out,
       not_512_out, not_513_out, not_514_out, not_515_out, not_516_out, not_517_out, not_518_out,
       not_519_out, not_520_out, not_521_out, not_522_out, not_523_out, not_524_out, not_525_out,
       not_526_out, not_527_out, not_528_out, not_530_out, not_531_out, not_532_out, not_533_out,
       not_534_out, not_535_out, not_536_out, not_537_out, not_538_out, not_539_out, not_540_out,
       not_541_out, not_542_out, not_543_out, not_544_out, not_545_out, not_546_out, not_547_out,
       not_548_out, not_549_out, not_550_out, not_551_out, not_552_out, not_553_out, not_554_out,
       not_555_out, not_556_out, not_557_out, not_558_out, not_559_out, not_560_out, not_561_out,
       not_563_out, not_564_out, not_565_out, not_566_out, not_567_out, not_568_out, not_569_out,
       not_570_out, not_571_out, not_572_out, not_573_out, not_574_out, not_575_out, not_576_out,
       not_577_out, not_578_out, not_579_out, not_580_out, not_581_out, not_582_out, not_583_out,
       not_584_out, not_585_out, not_586_out, not_587_out, not_588_out, not_589_out, not_590_out,
       not_591_out, not_592_out, not_593_out, not_594_out, not_596_out, not_597_out, not_598_out,
       not_599_out, not_600_out, not_601_out, not_602_out, not_603_out, not_604_out, not_605_out,
       not_606_out, not_607_out, not_608_out, not_609_out, not_610_out, not_611_out, not_612_out,
       not_613_out, not_614_out, not_615_out, not_616_out, not_617_out, not_618_out, not_619_out,
       not_620_out, not_621_out, not_622_out, not_623_out, not_624_out, not_625_out, not_626_out,
       not_627_out, not_629_out, not_630_out, not_631_out, not_632_out, not_633_out, not_634_out,
       not_635_out, not_636_out, not_637_out, not_638_out, not_639_out, not_640_out, not_641_out,
       not_642_out, not_643_out, not_644_out, not_645_out, not_646_out, not_647_out, not_648_out,
       not_649_out, not_650_out, not_651_out, not_652_out, not_653_out, not_654_out, not_655_out,
       not_656_out, not_657_out, not_658_out, not_659_out, not_660_out, not_662_out, not_663_out,
       not_664_out, not_665_out, not_666_out, not_667_out, not_668_out, not_669_out, not_670_out,
       not_671_out, not_672_out, not_673_out, not_674_out, not_675_out, not_676_out, not_677_out,
       not_678_out, not_679_out, not_680_out, not_681_out, not_682_out, not_683_out, not_684_out,
       not_685_out, not_686_out, not_687_out, not_688_out, not_689_out, not_690_out, not_691_out,
       not_692_out, not_693_out, not_695_out, not_696_out, not_697_out, not_698_out, not_699_out,
       not_700_out, not_701_out, not_702_out, not_703_out, not_704_out, not_705_out, not_706_out,
       not_707_out, not_708_out, not_709_out, not_710_out, not_711_out, not_712_out, not_713_out,
       not_714_out, not_715_out, not_716_out, not_717_out, not_718_out, not_719_out, not_720_out,
       not_721_out, not_722_out, not_723_out, not_724_out, not_725_out, not_726_out, not_728_out,
       not_729_out, not_730_out, not_731_out, not_732_out, not_733_out, not_734_out, not_735_out,
       not_736_out, not_737_out, not_738_out, not_739_out, not_740_out, not_741_out, not_742_out,
       not_743_out, not_744_out, not_745_out, not_746_out, not_747_out, not_748_out, not_749_out,
       not_750_out, not_751_out, not_752_out, not_753_out, not_754_out, not_755_out, not_756_out,
       not_757_out, not_758_out, not_759_out, not_761_out, not_762_out, not_763_out, not_764_out,
       not_765_out, not_766_out, not_767_out, not_768_out, not_769_out, not_770_out, not_771_out,
       not_772_out, not_773_out, not_774_out, not_775_out, not_776_out, not_777_out, not_778_out,
       not_779_out, not_780_out, not_781_out, not_782_out, not_783_out, not_784_out, not_785_out,
       not_786_out, not_787_out, not_788_out, not_789_out, not_790_out, not_791_out, not_792_out,
       not_794_out, not_795_out, not_796_out, not_797_out, not_798_out, not_799_out, not_800_out,
       not_801_out, not_802_out, not_803_out, not_804_out, not_805_out, not_806_out, not_807_out,
       not_808_out, not_809_out, not_810_out, not_811_out, not_812_out, not_813_out, not_814_out,
       not_815_out, not_816_out, not_817_out, not_818_out, not_819_out, not_820_out, not_821_out,
       not_822_out, not_823_out, not_824_out, not_825_out, not_827_out, not_828_out, not_829_out,
       not_830_out, not_831_out, not_832_out, not_833_out, not_834_out, not_835_out, not_836_out,
       not_837_out, not_838_out, not_839_out, not_840_out, not_841_out, not_842_out, not_843_out,
       not_844_out, not_845_out, not_846_out, not_847_out, not_848_out, not_849_out, not_850_out,
       not_851_out, not_852_out, not_853_out, not_854_out, not_855_out, not_856_out, not_857_out,
       not_858_out, not_860_out, not_861_out, not_862_out, not_863_out, not_864_out, not_865_out,
       not_866_out, not_867_out, not_868_out, not_869_out, not_870_out, not_871_out, not_872_out,
       not_873_out, not_874_out, not_875_out, not_876_out, not_877_out, not_878_out, not_879_out,
       not_880_out, not_881_out, not_882_out, not_883_out, not_884_out, not_885_out, not_886_out,
       not_887_out, not_888_out, not_889_out, not_890_out, not_891_out, not_893_out, not_894_out,
       not_895_out, not_896_out, not_897_out, not_898_out, not_899_out, not_900_out, not_901_out,
       not_902_out, not_903_out, not_904_out, not_905_out, not_906_out, not_907_out, not_908_out,
       not_909_out, not_910_out, not_911_out, not_912_out, not_913_out, not_914_out, not_915_out,
       not_916_out, not_917_out, not_918_out, not_919_out, not_920_out, not_921_out, not_922_out,
       not_923_out, not_924_out, not_926_out, not_927_out, not_928_out, not_929_out, not_930_out,
       not_931_out, not_932_out, not_933_out, not_934_out, not_935_out, not_936_out, not_937_out,
       not_938_out, not_939_out, not_940_out, not_941_out, not_942_out, not_943_out, not_944_out,
       not_945_out, not_946_out, not_947_out, not_948_out, not_949_out, not_950_out, not_951_out,
       not_952_out, not_953_out, not_954_out, not_955_out, not_956_out, not_957_out, not_959_out,
       not_960_out, not_961_out, not_962_out, not_963_out, not_964_out, not_965_out, not_966_out,
       not_967_out, not_968_out, not_969_out, not_970_out, not_971_out, not_972_out, not_973_out,
       not_974_out, not_975_out, not_976_out, not_977_out, not_978_out, not_979_out, not_980_out,
       not_981_out, not_982_out, not_983_out, not_984_out, not_985_out, not_986_out, not_987_out,
       not_988_out, not_989_out, not_990_out, not_992_out, not_993_out, not_994_out, not_995_out,
       not_996_out, not_997_out, not_998_out, not_999_out, not_1000_out, not_1001_out, not_1002_out,
       not_1003_out, not_1004_out, not_1005_out, not_1006_out, not_1007_out, not_1008_out, not_1009_out,
       not_1010_out, not_1011_out, not_1012_out, not_1013_out, not_1014_out, not_1015_out, not_1016_out,
       not_1017_out, not_1018_out, not_1019_out, not_1020_out, not_1021_out, not_1022_out, not_1023_out;
  wire [31:0] and_33_out, and_34_out, and_35_out, and_36_out, and_37_out, and_38_out, and_39_out, and_40_out,
       and_41_out, and_42_out, and_43_out, and_44_out, and_45_out, and_46_out, and_47_out, and_48_out,
       and_49_out, and_50_out, and_51_out, and_52_out, and_53_out, and_54_out, and_55_out, and_56_out,
       and_57_out, and_58_out, and_59_out, and_60_out, and_61_out, and_62_out, and_63_out, and_64_out,
       or_2_out, or_3_out, or_4_out, or_5_out, or_6_out, or_7_out, or_8_out, or_9_out, or_10_out, or_11_out,
       or_12_out, or_13_out, or_14_out, or_15_out, or_16_out, or_17_out, or_18_out, or_19_out, or_20_out,
       or_21_out, or_22_out, or_23_out, or_24_out, or_25_out, or_26_out, or_27_out, or_28_out, or_29_out,
       or_30_out, or_31_out;
  wire [31:31] and_1_out, and_2_out, and_3_out, and_4_out, and_5_out, and_6_out, and_7_out, and_8_out,
       and_9_out, and_10_out, and_11_out, and_12_out, and_13_out, and_14_out, and_15_out, and_16_out,
       and_17_out, and_18_out, and_19_out, and_20_out, and_21_out, and_22_out, and_23_out, and_24_out,
       and_25_out, and_26_out, and_27_out, and_28_out, and_29_out, and_30_out, and_31_out, and_32_out;

  not not_1 (not_1_out, Selector[0]);
  not not_2 (not_2_out, Selector[1]);
  not not_3 (not_3_out, Selector[2]);
  not not_4 (not_4_out, Selector[3]);
  not not_5 (not_5_out, Selector[4]);
  not not_6 (not_6_out, Selector[5]);
  not not_7 (not_7_out, Selector[6]);
  not not_8 (not_8_out, Selector[7]);
  not not_9 (not_9_out, Selector[8]);
  not not_10 (not_10_out, Selector[9]);
  not not_11 (not_11_out, Selector[10]);
  not not_12 (not_12_out, Selector[11]);
  not not_13 (not_13_out, Selector[12]);
  not not_14 (not_14_out, Selector[13]);
  not not_15 (not_15_out, Selector[14]);
  not not_16 (not_16_out, Selector[15]);
  not not_17 (not_17_out, Selector[16]);
  not not_18 (not_18_out, Selector[17]);
  not not_19 (not_19_out, Selector[18]);
  not not_20 (not_20_out, Selector[19]);
  not not_21 (not_21_out, Selector[20]);
  not not_22 (not_22_out, Selector[21]);
  not not_23 (not_23_out, Selector[22]);
  not not_24 (not_24_out, Selector[23]);
  not not_25 (not_25_out, Selector[24]);
  not not_26 (not_26_out, Selector[25]);
  not not_27 (not_27_out, Selector[26]);
  not not_28 (not_28_out, Selector[27]);
  not not_29 (not_29_out, Selector[28]);
  not not_30 (not_30_out, Selector[29]);
  not not_31 (not_31_out, Selector[30]);
  not not_32 (not_32_out, Selector[31]);
  not not_33 (not_33_out, Selector[0]);
  // NOT_Gate not_34 has open pins: in=Selector[1], out=open
  not not_35 (not_35_out, Selector[2]);
  not not_36 (not_36_out, Selector[3]);
  not not_37 (not_37_out, Selector[4]);
  not not_38 (not_38_out, Selector[5]);
  not not_39 (not_39_out, Selector[6]);
  not not_40 (not_40_out, Selector[7]);
  not not_41 (not_41_out, Selector[8]);
  not not_42 (not_42_out, Selector[9]);
  not not_43 (not_43_out, Selector[10]);
  not not_44 (not_44_out, Selector[11]);
  not not_45 (not_45_out, Selector[12]);
  not not_46 (not_46_out, Selector[13]);
  not not_47 (not_47_out, Selector[14]);
  not not_48 (not_48_out, Selector[15]);
  not not_49 (not_49_out, Selector[16]);
  not not_50 (not_50_out, Selector[17]);
  not not_51 (not_51_out, Selector[18]);
  not not_52 (not_52_out, Selector[19]);
  not not_53 (not_53_out, Selector[20]);
  not not_54 (not_54_out, Selector[21]);
  not not_55 (not_55_out, Selector[22]);
  not not_56 (not_56_out, Selector[23]);
  not not_57 (not_57_out, Selector[24]);
  not not_58 (not_58_out, Selector[25]);
  not not_59 (not_59_out, Selector[26]);
  not not_60 (not_60_out, Selector[27]);
  not not_61 (not_61_out, Selector[28]);
  not not_62 (not_62_out, Selector[29]);
  not not_63 (not_63_out, Selector[30]);
  not not_64 (not_64_out, Selector[31]);
  not not_65 (not_65_out, Selector[0]);
  not not_66 (not_66_out, Selector[1]);
  // NOT_Gate not_67 has open pins: in=Selector[2], out=open
  not not_68 (not_68_out, Selector[3]);
  not not_69 (not_69_out, Selector[4]);
  not not_70 (not_70_out, Selector[5]);
  not not_71 (not_71_out, Selector[6]);
  not not_72 (not_72_out, Selector[7]);
  not not_73 (not_73_out, Selector[8]);
  not not_74 (not_74_out, Selector[9]);
  not not_75 (not_75_out, Selector[10]);
  not not_76 (not_76_out, Selector[11]);
  not not_77 (not_77_out, Selector[12]);
  not not_78 (not_78_out, Selector[13]);
  not not_79 (not_79_out, Selector[14]);
  not not_80 (not_80_out, Selector[15]);
  not not_81 (not_81_out, Selector[16]);
  not not_82 (not_82_out, Selector[17]);
  not not_83 (not_83_out, Selector[18]);
  not not_84 (not_84_out, Selector[19]);
  not not_85 (not_85_out, Selector[20]);
  not not_86 (not_86_out, Selector[21]);
  not not_87 (not_87_out, Selector[22]);
  not not_88 (not_88_out, Selector[23]);
  not not_89 (not_89_out, Selector[24]);
  not not_90 (not_90_out, Selector[25]);
  not not_91 (not_91_out, Selector[26]);
  not not_92 (not_92_out, Selector[27]);
  not not_93 (not_93_out, Selector[28]);
  not not_94 (not_94_out, Selector[29]);
  not not_95 (not_95_out, Selector[30]);
  not not_96 (not_96_out, Selector[31]);
  not not_97 (not_97_out, Selector[0]);
  not not_98 (not_98_out, Selector[1]);
  not not_99 (not_99_out, Selector[2]);
  // NOT_Gate not_100 has open pins: in=Selector[3], out=open
  not not_101 (not_101_out, Selector[4]);
  not not_102 (not_102_out, Selector[5]);
  not not_103 (not_103_out, Selector[6]);
  not not_104 (not_104_out, Selector[7]);
  not not_105 (not_105_out, Selector[8]);
  not not_106 (not_106_out, Selector[9]);
  not not_107 (not_107_out, Selector[10]);
  not not_108 (not_108_out, Selector[11]);
  not not_109 (not_109_out, Selector[12]);
  not not_110 (not_110_out, Selector[13]);
  not not_111 (not_111_out, Selector[14]);
  not not_112 (not_112_out, Selector[15]);
  not not_113 (not_113_out, Selector[16]);
  not not_114 (not_114_out, Selector[17]);
  not not_115 (not_115_out, Selector[18]);
  not not_116 (not_116_out, Selector[19]);
  not not_117 (not_117_out, Selector[20]);
  not not_118 (not_118_out, Selector[21]);
  not not_119 (not_119_out, Selector[22]);
  not not_120 (not_120_out, Selector[23]);
  not not_121 (not_121_out, Selector[24]);
  not not_122 (not_122_out, Selector[25]);
  not not_123 (not_123_out, Selector[26]);
  not not_124 (not_124_out, Selector[27]);
  not not_125 (not_125_out, Selector[28]);
  not not_126 (not_126_out, Selector[29]);
  not not_127 (not_127_out, Selector[30]);
  not not_128 (not_128_out, Selector[31]);
  not not_129 (not_129_out, Selector[0]);
  not not_130 (not_130_out, Selector[1]);
  not not_131 (not_131_out, Selector[2]);
  not not_132 (not_132_out, Selector[3]);
  // NOT_Gate not_133 has open pins: in=Selector[4], out=open
  not not_134 (not_134_out, Selector[5]);
  not not_135 (not_135_out, Selector[6]);
  not not_136 (not_136_out, Selector[7]);
  not not_137 (not_137_out, Selector[8]);
  not not_138 (not_138_out, Selector[9]);
  not not_139 (not_139_out, Selector[10]);
  not not_140 (not_140_out, Selector[11]);
  not not_141 (not_141_out, Selector[12]);
  not not_142 (not_142_out, Selector[13]);
  not not_143 (not_143_out, Selector[14]);
  not not_144 (not_144_out, Selector[15]);
  not not_145 (not_145_out, Selector[16]);
  not not_146 (not_146_out, Selector[17]);
  not not_147 (not_147_out, Selector[18]);
  not not_148 (not_148_out, Selector[19]);
  not not_149 (not_149_out, Selector[20]);
  not not_150 (not_150_out, Selector[21]);
  not not_151 (not_151_out, Selector[22]);
  not not_152 (not_152_out, Selector[23]);
  not not_153 (not_153_out, Selector[24]);
  not not_154 (not_154_out, Selector[25]);
  not not_155 (not_155_out, Selector[26]);
  not not_156 (not_156_out, Selector[27]);
  not not_157 (not_157_out, Selector[28]);
  not not_158 (not_158_out, Selector[29]);
  not not_159 (not_159_out, Selector[30]);
  not not_160 (not_160_out, Selector[31]);
  not not_161 (not_161_out, Selector[0]);
  not not_162 (not_162_out, Selector[1]);
  not not_163 (not_163_out, Selector[2]);
  not not_164 (not_164_out, Selector[3]);
  // NOT_Gate not_165 has open pins: in=Selector[4], out=open
  not not_166 (not_166_out, Selector[5]);
  not not_167 (not_167_out, Selector[6]);
  not not_168 (not_168_out, Selector[7]);
  not not_169 (not_169_out, Selector[8]);
  not not_170 (not_170_out, Selector[9]);
  not not_171 (not_171_out, Selector[10]);
  not not_172 (not_172_out, Selector[11]);
  not not_173 (not_173_out, Selector[12]);
  not not_174 (not_174_out, Selector[13]);
  not not_175 (not_175_out, Selector[14]);
  not not_176 (not_176_out, Selector[15]);
  not not_177 (not_177_out, Selector[16]);
  not not_178 (not_178_out, Selector[17]);
  not not_179 (not_179_out, Selector[18]);
  not not_180 (not_180_out, Selector[19]);
  not not_181 (not_181_out, Selector[20]);
  not not_182 (not_182_out, Selector[21]);
  not not_183 (not_183_out, Selector[22]);
  not not_184 (not_184_out, Selector[23]);
  not not_185 (not_185_out, Selector[24]);
  not not_186 (not_186_out, Selector[25]);
  not not_187 (not_187_out, Selector[26]);
  not not_188 (not_188_out, Selector[27]);
  not not_189 (not_189_out, Selector[28]);
  not not_190 (not_190_out, Selector[29]);
  not not_191 (not_191_out, Selector[30]);
  not not_192 (not_192_out, Selector[31]);
  not not_193 (not_193_out, Selector[0]);
  not not_194 (not_194_out, Selector[1]);
  not not_195 (not_195_out, Selector[2]);
  not not_196 (not_196_out, Selector[3]);
  not not_197 (not_197_out, Selector[4]);
  not not_198 (not_198_out, Selector[5]);
  // NOT_Gate not_199 has open pins: in=Selector[6], out=open
  not not_200 (not_200_out, Selector[7]);
  not not_201 (not_201_out, Selector[8]);
  not not_202 (not_202_out, Selector[9]);
  not not_203 (not_203_out, Selector[10]);
  not not_204 (not_204_out, Selector[11]);
  not not_205 (not_205_out, Selector[12]);
  not not_206 (not_206_out, Selector[13]);
  not not_207 (not_207_out, Selector[14]);
  not not_208 (not_208_out, Selector[15]);
  not not_209 (not_209_out, Selector[16]);
  not not_210 (not_210_out, Selector[17]);
  not not_211 (not_211_out, Selector[18]);
  not not_212 (not_212_out, Selector[19]);
  not not_213 (not_213_out, Selector[20]);
  not not_214 (not_214_out, Selector[21]);
  not not_215 (not_215_out, Selector[22]);
  not not_216 (not_216_out, Selector[23]);
  not not_217 (not_217_out, Selector[24]);
  not not_218 (not_218_out, Selector[25]);
  not not_219 (not_219_out, Selector[26]);
  not not_220 (not_220_out, Selector[27]);
  not not_221 (not_221_out, Selector[28]);
  not not_222 (not_222_out, Selector[29]);
  not not_223 (not_223_out, Selector[30]);
  not not_224 (not_224_out, Selector[31]);
  not not_225 (not_225_out, Selector[0]);
  not not_226 (not_226_out, Selector[1]);
  not not_227 (not_227_out, Selector[2]);
  not not_228 (not_228_out, Selector[3]);
  not not_229 (not_229_out, Selector[4]);
  not not_230 (not_230_out, Selector[5]);
  not not_231 (not_231_out, Selector[6]);
  // NOT_Gate not_232 has open pins: in=Selector[7], out=open
  not not_233 (not_233_out, Selector[8]);
  not not_234 (not_234_out, Selector[9]);
  not not_235 (not_235_out, Selector[10]);
  not not_236 (not_236_out, Selector[11]);
  not not_237 (not_237_out, Selector[12]);
  not not_238 (not_238_out, Selector[13]);
  not not_239 (not_239_out, Selector[14]);
  not not_240 (not_240_out, Selector[15]);
  not not_241 (not_241_out, Selector[16]);
  not not_242 (not_242_out, Selector[17]);
  not not_243 (not_243_out, Selector[18]);
  not not_244 (not_244_out, Selector[19]);
  not not_245 (not_245_out, Selector[20]);
  not not_246 (not_246_out, Selector[21]);
  not not_247 (not_247_out, Selector[22]);
  not not_248 (not_248_out, Selector[23]);
  not not_249 (not_249_out, Selector[24]);
  not not_250 (not_250_out, Selector[25]);
  not not_251 (not_251_out, Selector[26]);
  not not_252 (not_252_out, Selector[27]);
  not not_253 (not_253_out, Selector[28]);
  not not_254 (not_254_out, Selector[29]);
  not not_255 (not_255_out, Selector[30]);
  not not_256 (not_256_out, Selector[31]);
  not not_257 (not_257_out, Selector[0]);
  not not_258 (not_258_out, Selector[1]);
  not not_259 (not_259_out, Selector[2]);
  not not_260 (not_260_out, Selector[3]);
  not not_261 (not_261_out, Selector[4]);
  not not_262 (not_262_out, Selector[5]);
  not not_263 (not_263_out, Selector[6]);
  not not_264 (not_264_out, Selector[7]);
  // NOT_Gate not_265 has open pins: in=Selector[8], out=open
  not not_266 (not_266_out, Selector[9]);
  not not_267 (not_267_out, Selector[10]);
  not not_268 (not_268_out, Selector[11]);
  not not_269 (not_269_out, Selector[12]);
  not not_270 (not_270_out, Selector[13]);
  not not_271 (not_271_out, Selector[14]);
  not not_272 (not_272_out, Selector[15]);
  not not_273 (not_273_out, Selector[16]);
  not not_274 (not_274_out, Selector[17]);
  not not_275 (not_275_out, Selector[18]);
  not not_276 (not_276_out, Selector[19]);
  not not_277 (not_277_out, Selector[20]);
  not not_278 (not_278_out, Selector[21]);
  not not_279 (not_279_out, Selector[22]);
  not not_280 (not_280_out, Selector[23]);
  not not_281 (not_281_out, Selector[24]);
  not not_282 (not_282_out, Selector[25]);
  not not_283 (not_283_out, Selector[26]);
  not not_284 (not_284_out, Selector[27]);
  not not_285 (not_285_out, Selector[28]);
  not not_286 (not_286_out, Selector[29]);
  not not_287 (not_287_out, Selector[30]);
  not not_288 (not_288_out, Selector[31]);
  not not_289 (not_289_out, Selector[0]);
  not not_290 (not_290_out, Selector[1]);
  not not_291 (not_291_out, Selector[2]);
  not not_292 (not_292_out, Selector[3]);
  not not_293 (not_293_out, Selector[4]);
  not not_294 (not_294_out, Selector[5]);
  not not_295 (not_295_out, Selector[6]);
  not not_296 (not_296_out, Selector[7]);
  not not_297 (not_297_out, Selector[8]);
  // NOT_Gate not_298 has open pins: in=Selector[9], out=open
  not not_299 (not_299_out, Selector[10]);
  not not_300 (not_300_out, Selector[11]);
  not not_301 (not_301_out, Selector[12]);
  not not_302 (not_302_out, Selector[13]);
  not not_303 (not_303_out, Selector[14]);
  not not_304 (not_304_out, Selector[15]);
  not not_305 (not_305_out, Selector[16]);
  not not_306 (not_306_out, Selector[17]);
  not not_307 (not_307_out, Selector[18]);
  not not_308 (not_308_out, Selector[19]);
  not not_309 (not_309_out, Selector[20]);
  not not_310 (not_310_out, Selector[21]);
  not not_311 (not_311_out, Selector[22]);
  not not_312 (not_312_out, Selector[23]);
  not not_313 (not_313_out, Selector[24]);
  not not_314 (not_314_out, Selector[25]);
  not not_315 (not_315_out, Selector[26]);
  not not_316 (not_316_out, Selector[27]);
  not not_317 (not_317_out, Selector[28]);
  not not_318 (not_318_out, Selector[29]);
  not not_319 (not_319_out, Selector[30]);
  not not_320 (not_320_out, Selector[31]);
  not not_321 (not_321_out, Selector[0]);
  not not_322 (not_322_out, Selector[1]);
  not not_323 (not_323_out, Selector[2]);
  not not_324 (not_324_out, Selector[3]);
  not not_325 (not_325_out, Selector[4]);
  not not_326 (not_326_out, Selector[5]);
  not not_327 (not_327_out, Selector[6]);
  not not_328 (not_328_out, Selector[7]);
  not not_329 (not_329_out, Selector[8]);
  not not_330 (not_330_out, Selector[9]);
  // NOT_Gate not_331 has open pins: in=Selector[10], out=open
  not not_332 (not_332_out, Selector[11]);
  not not_333 (not_333_out, Selector[12]);
  not not_334 (not_334_out, Selector[13]);
  not not_335 (not_335_out, Selector[14]);
  not not_336 (not_336_out, Selector[15]);
  not not_337 (not_337_out, Selector[16]);
  not not_338 (not_338_out, Selector[17]);
  not not_339 (not_339_out, Selector[18]);
  not not_340 (not_340_out, Selector[19]);
  not not_341 (not_341_out, Selector[20]);
  not not_342 (not_342_out, Selector[21]);
  not not_343 (not_343_out, Selector[22]);
  not not_344 (not_344_out, Selector[23]);
  not not_345 (not_345_out, Selector[24]);
  not not_346 (not_346_out, Selector[25]);
  not not_347 (not_347_out, Selector[26]);
  not not_348 (not_348_out, Selector[27]);
  not not_349 (not_349_out, Selector[28]);
  not not_350 (not_350_out, Selector[29]);
  not not_351 (not_351_out, Selector[30]);
  not not_352 (not_352_out, Selector[31]);
  not not_353 (not_353_out, Selector[0]);
  not not_354 (not_354_out, Selector[1]);
  not not_355 (not_355_out, Selector[2]);
  not not_356 (not_356_out, Selector[3]);
  not not_357 (not_357_out, Selector[4]);
  not not_358 (not_358_out, Selector[5]);
  not not_359 (not_359_out, Selector[6]);
  not not_360 (not_360_out, Selector[7]);
  not not_361 (not_361_out, Selector[8]);
  not not_362 (not_362_out, Selector[9]);
  not not_363 (not_363_out, Selector[10]);
  // NOT_Gate not_364 has open pins: in=Selector[11], out=open
  not not_365 (not_365_out, Selector[12]);
  not not_366 (not_366_out, Selector[13]);
  not not_367 (not_367_out, Selector[14]);
  not not_368 (not_368_out, Selector[15]);
  not not_369 (not_369_out, Selector[16]);
  not not_370 (not_370_out, Selector[17]);
  not not_371 (not_371_out, Selector[18]);
  not not_372 (not_372_out, Selector[19]);
  not not_373 (not_373_out, Selector[20]);
  not not_374 (not_374_out, Selector[21]);
  not not_375 (not_375_out, Selector[22]);
  not not_376 (not_376_out, Selector[23]);
  not not_377 (not_377_out, Selector[24]);
  not not_378 (not_378_out, Selector[25]);
  not not_379 (not_379_out, Selector[26]);
  not not_380 (not_380_out, Selector[27]);
  not not_381 (not_381_out, Selector[28]);
  not not_382 (not_382_out, Selector[29]);
  not not_383 (not_383_out, Selector[30]);
  not not_384 (not_384_out, Selector[31]);
  not not_385 (not_385_out, Selector[0]);
  not not_386 (not_386_out, Selector[1]);
  not not_387 (not_387_out, Selector[2]);
  not not_388 (not_388_out, Selector[3]);
  not not_389 (not_389_out, Selector[4]);
  not not_390 (not_390_out, Selector[5]);
  not not_391 (not_391_out, Selector[6]);
  not not_392 (not_392_out, Selector[7]);
  not not_393 (not_393_out, Selector[8]);
  not not_394 (not_394_out, Selector[9]);
  not not_395 (not_395_out, Selector[10]);
  not not_396 (not_396_out, Selector[11]);
  // NOT_Gate not_397 has open pins: in=Selector[12], out=open
  not not_398 (not_398_out, Selector[13]);
  not not_399 (not_399_out, Selector[14]);
  not not_400 (not_400_out, Selector[15]);
  not not_401 (not_401_out, Selector[16]);
  not not_402 (not_402_out, Selector[17]);
  not not_403 (not_403_out, Selector[18]);
  not not_404 (not_404_out, Selector[19]);
  not not_405 (not_405_out, Selector[20]);
  not not_406 (not_406_out, Selector[21]);
  not not_407 (not_407_out, Selector[22]);
  not not_408 (not_408_out, Selector[23]);
  not not_409 (not_409_out, Selector[24]);
  not not_410 (not_410_out, Selector[25]);
  not not_411 (not_411_out, Selector[26]);
  not not_412 (not_412_out, Selector[27]);
  not not_413 (not_413_out, Selector[28]);
  not not_414 (not_414_out, Selector[29]);
  not not_415 (not_415_out, Selector[30]);
  not not_416 (not_416_out, Selector[31]);
  not not_417 (not_417_out, Selector[0]);
  not not_418 (not_418_out, Selector[1]);
  not not_419 (not_419_out, Selector[2]);
  not not_420 (not_420_out, Selector[3]);
  not not_421 (not_421_out, Selector[4]);
  not not_422 (not_422_out, Selector[5]);
  not not_423 (not_423_out, Selector[6]);
  not not_424 (not_424_out, Selector[7]);
  not not_425 (not_425_out, Selector[8]);
  not not_426 (not_426_out, Selector[9]);
  not not_427 (not_427_out, Selector[10]);
  not not_428 (not_428_out, Selector[11]);
  not not_429 (not_429_out, Selector[12]);
  // NOT_Gate not_430 has open pins: in=Selector[13], out=open
  not not_431 (not_431_out, Selector[14]);
  not not_432 (not_432_out, Selector[15]);
  not not_433 (not_433_out, Selector[16]);
  not not_434 (not_434_out, Selector[17]);
  not not_435 (not_435_out, Selector[18]);
  not not_436 (not_436_out, Selector[19]);
  not not_437 (not_437_out, Selector[20]);
  not not_438 (not_438_out, Selector[21]);
  not not_439 (not_439_out, Selector[22]);
  not not_440 (not_440_out, Selector[23]);
  not not_441 (not_441_out, Selector[24]);
  not not_442 (not_442_out, Selector[25]);
  not not_443 (not_443_out, Selector[26]);
  not not_444 (not_444_out, Selector[27]);
  not not_445 (not_445_out, Selector[28]);
  not not_446 (not_446_out, Selector[29]);
  not not_447 (not_447_out, Selector[30]);
  not not_448 (not_448_out, Selector[31]);
  not not_449 (not_449_out, Selector[0]);
  not not_450 (not_450_out, Selector[1]);
  not not_451 (not_451_out, Selector[2]);
  not not_452 (not_452_out, Selector[3]);
  not not_453 (not_453_out, Selector[4]);
  not not_454 (not_454_out, Selector[5]);
  not not_455 (not_455_out, Selector[6]);
  not not_456 (not_456_out, Selector[7]);
  not not_457 (not_457_out, Selector[8]);
  not not_458 (not_458_out, Selector[9]);
  not not_459 (not_459_out, Selector[10]);
  not not_460 (not_460_out, Selector[11]);
  not not_461 (not_461_out, Selector[12]);
  not not_462 (not_462_out, Selector[13]);
  // NOT_Gate not_463 has open pins: in=Selector[14], out=open
  not not_464 (not_464_out, Selector[15]);
  not not_465 (not_465_out, Selector[16]);
  not not_466 (not_466_out, Selector[17]);
  not not_467 (not_467_out, Selector[18]);
  not not_468 (not_468_out, Selector[19]);
  not not_469 (not_469_out, Selector[20]);
  not not_470 (not_470_out, Selector[21]);
  not not_471 (not_471_out, Selector[22]);
  not not_472 (not_472_out, Selector[23]);
  not not_473 (not_473_out, Selector[24]);
  not not_474 (not_474_out, Selector[25]);
  not not_475 (not_475_out, Selector[26]);
  not not_476 (not_476_out, Selector[27]);
  not not_477 (not_477_out, Selector[28]);
  not not_478 (not_478_out, Selector[29]);
  not not_479 (not_479_out, Selector[30]);
  not not_480 (not_480_out, Selector[31]);
  not not_481 (not_481_out, Selector[0]);
  not not_482 (not_482_out, Selector[1]);
  not not_483 (not_483_out, Selector[2]);
  not not_484 (not_484_out, Selector[3]);
  not not_485 (not_485_out, Selector[4]);
  not not_486 (not_486_out, Selector[5]);
  not not_487 (not_487_out, Selector[6]);
  not not_488 (not_488_out, Selector[7]);
  not not_489 (not_489_out, Selector[8]);
  not not_490 (not_490_out, Selector[9]);
  not not_491 (not_491_out, Selector[10]);
  not not_492 (not_492_out, Selector[11]);
  not not_493 (not_493_out, Selector[12]);
  not not_494 (not_494_out, Selector[13]);
  not not_495 (not_495_out, Selector[14]);
  // NOT_Gate not_496 has open pins: in=Selector[15], out=open
  not not_497 (not_497_out, Selector[16]);
  not not_498 (not_498_out, Selector[17]);
  not not_499 (not_499_out, Selector[18]);
  not not_500 (not_500_out, Selector[19]);
  not not_501 (not_501_out, Selector[20]);
  not not_502 (not_502_out, Selector[21]);
  not not_503 (not_503_out, Selector[22]);
  not not_504 (not_504_out, Selector[23]);
  not not_505 (not_505_out, Selector[24]);
  not not_506 (not_506_out, Selector[25]);
  not not_507 (not_507_out, Selector[26]);
  not not_508 (not_508_out, Selector[27]);
  not not_509 (not_509_out, Selector[28]);
  not not_510 (not_510_out, Selector[29]);
  not not_511 (not_511_out, Selector[30]);
  not not_512 (not_512_out, Selector[31]);
  not not_513 (not_513_out, Selector[0]);
  not not_514 (not_514_out, Selector[1]);
  not not_515 (not_515_out, Selector[2]);
  not not_516 (not_516_out, Selector[3]);
  not not_517 (not_517_out, Selector[4]);
  not not_518 (not_518_out, Selector[5]);
  not not_519 (not_519_out, Selector[6]);
  not not_520 (not_520_out, Selector[7]);
  not not_521 (not_521_out, Selector[8]);
  not not_522 (not_522_out, Selector[9]);
  not not_523 (not_523_out, Selector[10]);
  not not_524 (not_524_out, Selector[11]);
  not not_525 (not_525_out, Selector[12]);
  not not_526 (not_526_out, Selector[13]);
  not not_527 (not_527_out, Selector[14]);
  not not_528 (not_528_out, Selector[15]);
  // NOT_Gate not_529 has open pins: in=Selector[16], out=open
  not not_530 (not_530_out, Selector[17]);
  not not_531 (not_531_out, Selector[18]);
  not not_532 (not_532_out, Selector[19]);
  not not_533 (not_533_out, Selector[20]);
  not not_534 (not_534_out, Selector[21]);
  not not_535 (not_535_out, Selector[22]);
  not not_536 (not_536_out, Selector[23]);
  not not_537 (not_537_out, Selector[24]);
  not not_538 (not_538_out, Selector[25]);
  not not_539 (not_539_out, Selector[26]);
  not not_540 (not_540_out, Selector[27]);
  not not_541 (not_541_out, Selector[28]);
  not not_542 (not_542_out, Selector[29]);
  not not_543 (not_543_out, Selector[30]);
  not not_544 (not_544_out, Selector[31]);
  not not_545 (not_545_out, Selector[0]);
  not not_546 (not_546_out, Selector[1]);
  not not_547 (not_547_out, Selector[2]);
  not not_548 (not_548_out, Selector[3]);
  not not_549 (not_549_out, Selector[4]);
  not not_550 (not_550_out, Selector[5]);
  not not_551 (not_551_out, Selector[6]);
  not not_552 (not_552_out, Selector[7]);
  not not_553 (not_553_out, Selector[8]);
  not not_554 (not_554_out, Selector[9]);
  not not_555 (not_555_out, Selector[10]);
  not not_556 (not_556_out, Selector[11]);
  not not_557 (not_557_out, Selector[12]);
  not not_558 (not_558_out, Selector[13]);
  not not_559 (not_559_out, Selector[14]);
  not not_560 (not_560_out, Selector[15]);
  not not_561 (not_561_out, Selector[16]);
  // NOT_Gate not_562 has open pins: in=Selector[17], out=open
  not not_563 (not_563_out, Selector[18]);
  not not_564 (not_564_out, Selector[19]);
  not not_565 (not_565_out, Selector[20]);
  not not_566 (not_566_out, Selector[21]);
  not not_567 (not_567_out, Selector[22]);
  not not_568 (not_568_out, Selector[23]);
  not not_569 (not_569_out, Selector[24]);
  not not_570 (not_570_out, Selector[25]);
  not not_571 (not_571_out, Selector[26]);
  not not_572 (not_572_out, Selector[27]);
  not not_573 (not_573_out, Selector[28]);
  not not_574 (not_574_out, Selector[29]);
  not not_575 (not_575_out, Selector[30]);
  not not_576 (not_576_out, Selector[31]);
  not not_577 (not_577_out, Selector[0]);
  not not_578 (not_578_out, Selector[1]);
  not not_579 (not_579_out, Selector[2]);
  not not_580 (not_580_out, Selector[3]);
  not not_581 (not_581_out, Selector[4]);
  not not_582 (not_582_out, Selector[5]);
  not not_583 (not_583_out, Selector[6]);
  not not_584 (not_584_out, Selector[7]);
  not not_585 (not_585_out, Selector[8]);
  not not_586 (not_586_out, Selector[9]);
  not not_587 (not_587_out, Selector[10]);
  not not_588 (not_588_out, Selector[11]);
  not not_589 (not_589_out, Selector[12]);
  not not_590 (not_590_out, Selector[13]);
  not not_591 (not_591_out, Selector[14]);
  not not_592 (not_592_out, Selector[15]);
  not not_593 (not_593_out, Selector[16]);
  not not_594 (not_594_out, Selector[17]);
  // NOT_Gate not_595 has open pins: in=Selector[18], out=open
  not not_596 (not_596_out, Selector[19]);
  not not_597 (not_597_out, Selector[20]);
  not not_598 (not_598_out, Selector[21]);
  not not_599 (not_599_out, Selector[22]);
  not not_600 (not_600_out, Selector[23]);
  not not_601 (not_601_out, Selector[24]);
  not not_602 (not_602_out, Selector[25]);
  not not_603 (not_603_out, Selector[26]);
  not not_604 (not_604_out, Selector[27]);
  not not_605 (not_605_out, Selector[28]);
  not not_606 (not_606_out, Selector[29]);
  not not_607 (not_607_out, Selector[30]);
  not not_608 (not_608_out, Selector[31]);
  not not_609 (not_609_out, Selector[0]);
  not not_610 (not_610_out, Selector[1]);
  not not_611 (not_611_out, Selector[2]);
  not not_612 (not_612_out, Selector[3]);
  not not_613 (not_613_out, Selector[4]);
  not not_614 (not_614_out, Selector[5]);
  not not_615 (not_615_out, Selector[6]);
  not not_616 (not_616_out, Selector[7]);
  not not_617 (not_617_out, Selector[8]);
  not not_618 (not_618_out, Selector[9]);
  not not_619 (not_619_out, Selector[10]);
  not not_620 (not_620_out, Selector[11]);
  not not_621 (not_621_out, Selector[12]);
  not not_622 (not_622_out, Selector[13]);
  not not_623 (not_623_out, Selector[14]);
  not not_624 (not_624_out, Selector[15]);
  not not_625 (not_625_out, Selector[16]);
  not not_626 (not_626_out, Selector[17]);
  not not_627 (not_627_out, Selector[18]);
  // NOT_Gate not_628 has open pins: in=Selector[19], out=open
  not not_629 (not_629_out, Selector[20]);
  not not_630 (not_630_out, Selector[21]);
  not not_631 (not_631_out, Selector[22]);
  not not_632 (not_632_out, Selector[23]);
  not not_633 (not_633_out, Selector[24]);
  not not_634 (not_634_out, Selector[25]);
  not not_635 (not_635_out, Selector[26]);
  not not_636 (not_636_out, Selector[27]);
  not not_637 (not_637_out, Selector[28]);
  not not_638 (not_638_out, Selector[29]);
  not not_639 (not_639_out, Selector[30]);
  not not_640 (not_640_out, Selector[31]);
  not not_641 (not_641_out, Selector[0]);
  not not_642 (not_642_out, Selector[1]);
  not not_643 (not_643_out, Selector[2]);
  not not_644 (not_644_out, Selector[3]);
  not not_645 (not_645_out, Selector[4]);
  not not_646 (not_646_out, Selector[5]);
  not not_647 (not_647_out, Selector[6]);
  not not_648 (not_648_out, Selector[7]);
  not not_649 (not_649_out, Selector[8]);
  not not_650 (not_650_out, Selector[9]);
  not not_651 (not_651_out, Selector[10]);
  not not_652 (not_652_out, Selector[11]);
  not not_653 (not_653_out, Selector[12]);
  not not_654 (not_654_out, Selector[13]);
  not not_655 (not_655_out, Selector[14]);
  not not_656 (not_656_out, Selector[15]);
  not not_657 (not_657_out, Selector[16]);
  not not_658 (not_658_out, Selector[17]);
  not not_659 (not_659_out, Selector[18]);
  not not_660 (not_660_out, Selector[19]);
  // NOT_Gate not_661 has open pins: in=Selector[20], out=open
  not not_662 (not_662_out, Selector[21]);
  not not_663 (not_663_out, Selector[22]);
  not not_664 (not_664_out, Selector[23]);
  not not_665 (not_665_out, Selector[24]);
  not not_666 (not_666_out, Selector[25]);
  not not_667 (not_667_out, Selector[26]);
  not not_668 (not_668_out, Selector[27]);
  not not_669 (not_669_out, Selector[28]);
  not not_670 (not_670_out, Selector[29]);
  not not_671 (not_671_out, Selector[30]);
  not not_672 (not_672_out, Selector[31]);
  not not_673 (not_673_out, Selector[0]);
  not not_674 (not_674_out, Selector[1]);
  not not_675 (not_675_out, Selector[2]);
  not not_676 (not_676_out, Selector[3]);
  not not_677 (not_677_out, Selector[4]);
  not not_678 (not_678_out, Selector[5]);
  not not_679 (not_679_out, Selector[6]);
  not not_680 (not_680_out, Selector[7]);
  not not_681 (not_681_out, Selector[8]);
  not not_682 (not_682_out, Selector[9]);
  not not_683 (not_683_out, Selector[10]);
  not not_684 (not_684_out, Selector[11]);
  not not_685 (not_685_out, Selector[12]);
  not not_686 (not_686_out, Selector[13]);
  not not_687 (not_687_out, Selector[14]);
  not not_688 (not_688_out, Selector[15]);
  not not_689 (not_689_out, Selector[16]);
  not not_690 (not_690_out, Selector[17]);
  not not_691 (not_691_out, Selector[18]);
  not not_692 (not_692_out, Selector[19]);
  not not_693 (not_693_out, Selector[20]);
  // NOT_Gate not_694 has open pins: in=Selector[21], out=open
  not not_695 (not_695_out, Selector[22]);
  not not_696 (not_696_out, Selector[23]);
  not not_697 (not_697_out, Selector[24]);
  not not_698 (not_698_out, Selector[25]);
  not not_699 (not_699_out, Selector[26]);
  not not_700 (not_700_out, Selector[27]);
  not not_701 (not_701_out, Selector[28]);
  not not_702 (not_702_out, Selector[29]);
  not not_703 (not_703_out, Selector[30]);
  not not_704 (not_704_out, Selector[31]);
  not not_705 (not_705_out, Selector[0]);
  not not_706 (not_706_out, Selector[1]);
  not not_707 (not_707_out, Selector[2]);
  not not_708 (not_708_out, Selector[3]);
  not not_709 (not_709_out, Selector[4]);
  not not_710 (not_710_out, Selector[5]);
  not not_711 (not_711_out, Selector[6]);
  not not_712 (not_712_out, Selector[7]);
  not not_713 (not_713_out, Selector[8]);
  not not_714 (not_714_out, Selector[9]);
  not not_715 (not_715_out, Selector[10]);
  not not_716 (not_716_out, Selector[11]);
  not not_717 (not_717_out, Selector[12]);
  not not_718 (not_718_out, Selector[13]);
  not not_719 (not_719_out, Selector[14]);
  not not_720 (not_720_out, Selector[15]);
  not not_721 (not_721_out, Selector[16]);
  not not_722 (not_722_out, Selector[17]);
  not not_723 (not_723_out, Selector[18]);
  not not_724 (not_724_out, Selector[19]);
  not not_725 (not_725_out, Selector[20]);
  not not_726 (not_726_out, Selector[21]);
  // NOT_Gate not_727 has open pins: in=Selector[22], out=open
  not not_728 (not_728_out, Selector[23]);
  not not_729 (not_729_out, Selector[24]);
  not not_730 (not_730_out, Selector[25]);
  not not_731 (not_731_out, Selector[26]);
  not not_732 (not_732_out, Selector[27]);
  not not_733 (not_733_out, Selector[28]);
  not not_734 (not_734_out, Selector[29]);
  not not_735 (not_735_out, Selector[30]);
  not not_736 (not_736_out, Selector[31]);
  not not_737 (not_737_out, Selector[0]);
  not not_738 (not_738_out, Selector[1]);
  not not_739 (not_739_out, Selector[2]);
  not not_740 (not_740_out, Selector[3]);
  not not_741 (not_741_out, Selector[4]);
  not not_742 (not_742_out, Selector[5]);
  not not_743 (not_743_out, Selector[6]);
  not not_744 (not_744_out, Selector[7]);
  not not_745 (not_745_out, Selector[8]);
  not not_746 (not_746_out, Selector[9]);
  not not_747 (not_747_out, Selector[10]);
  not not_748 (not_748_out, Selector[11]);
  not not_749 (not_749_out, Selector[12]);
  not not_750 (not_750_out, Selector[13]);
  not not_751 (not_751_out, Selector[14]);
  not not_752 (not_752_out, Selector[15]);
  not not_753 (not_753_out, Selector[16]);
  not not_754 (not_754_out, Selector[17]);
  not not_755 (not_755_out, Selector[18]);
  not not_756 (not_756_out, Selector[19]);
  not not_757 (not_757_out, Selector[20]);
  not not_758 (not_758_out, Selector[21]);
  not not_759 (not_759_out, Selector[22]);
  // NOT_Gate not_760 has open pins: in=Selector[23], out=open
  not not_761 (not_761_out, Selector[24]);
  not not_762 (not_762_out, Selector[25]);
  not not_763 (not_763_out, Selector[26]);
  not not_764 (not_764_out, Selector[27]);
  not not_765 (not_765_out, Selector[28]);
  not not_766 (not_766_out, Selector[29]);
  not not_767 (not_767_out, Selector[30]);
  not not_768 (not_768_out, Selector[31]);
  not not_769 (not_769_out, Selector[0]);
  not not_770 (not_770_out, Selector[1]);
  not not_771 (not_771_out, Selector[2]);
  not not_772 (not_772_out, Selector[3]);
  not not_773 (not_773_out, Selector[4]);
  not not_774 (not_774_out, Selector[5]);
  not not_775 (not_775_out, Selector[6]);
  not not_776 (not_776_out, Selector[7]);
  not not_777 (not_777_out, Selector[8]);
  not not_778 (not_778_out, Selector[9]);
  not not_779 (not_779_out, Selector[10]);
  not not_780 (not_780_out, Selector[11]);
  not not_781 (not_781_out, Selector[12]);
  not not_782 (not_782_out, Selector[13]);
  not not_783 (not_783_out, Selector[14]);
  not not_784 (not_784_out, Selector[15]);
  not not_785 (not_785_out, Selector[16]);
  not not_786 (not_786_out, Selector[17]);
  not not_787 (not_787_out, Selector[18]);
  not not_788 (not_788_out, Selector[19]);
  not not_789 (not_789_out, Selector[20]);
  not not_790 (not_790_out, Selector[21]);
  not not_791 (not_791_out, Selector[22]);
  not not_792 (not_792_out, Selector[23]);
  // NOT_Gate not_793 has open pins: in=Selector[24], out=open
  not not_794 (not_794_out, Selector[25]);
  not not_795 (not_795_out, Selector[26]);
  not not_796 (not_796_out, Selector[27]);
  not not_797 (not_797_out, Selector[28]);
  not not_798 (not_798_out, Selector[29]);
  not not_799 (not_799_out, Selector[30]);
  not not_800 (not_800_out, Selector[31]);
  not not_801 (not_801_out, Selector[0]);
  not not_802 (not_802_out, Selector[1]);
  not not_803 (not_803_out, Selector[2]);
  not not_804 (not_804_out, Selector[3]);
  not not_805 (not_805_out, Selector[4]);
  not not_806 (not_806_out, Selector[5]);
  not not_807 (not_807_out, Selector[6]);
  not not_808 (not_808_out, Selector[7]);
  not not_809 (not_809_out, Selector[8]);
  not not_810 (not_810_out, Selector[9]);
  not not_811 (not_811_out, Selector[10]);
  not not_812 (not_812_out, Selector[11]);
  not not_813 (not_813_out, Selector[12]);
  not not_814 (not_814_out, Selector[13]);
  not not_815 (not_815_out, Selector[14]);
  not not_816 (not_816_out, Selector[15]);
  not not_817 (not_817_out, Selector[16]);
  not not_818 (not_818_out, Selector[17]);
  not not_819 (not_819_out, Selector[18]);
  not not_820 (not_820_out, Selector[19]);
  not not_821 (not_821_out, Selector[20]);
  not not_822 (not_822_out, Selector[21]);
  not not_823 (not_823_out, Selector[22]);
  not not_824 (not_824_out, Selector[23]);
  not not_825 (not_825_out, Selector[24]);
  // NOT_Gate not_826 has open pins: in=Selector[25], out=open
  not not_827 (not_827_out, Selector[26]);
  not not_828 (not_828_out, Selector[27]);
  not not_829 (not_829_out, Selector[28]);
  not not_830 (not_830_out, Selector[29]);
  not not_831 (not_831_out, Selector[30]);
  not not_832 (not_832_out, Selector[31]);
  not not_833 (not_833_out, Selector[0]);
  not not_834 (not_834_out, Selector[1]);
  not not_835 (not_835_out, Selector[2]);
  not not_836 (not_836_out, Selector[3]);
  not not_837 (not_837_out, Selector[4]);
  not not_838 (not_838_out, Selector[5]);
  not not_839 (not_839_out, Selector[6]);
  not not_840 (not_840_out, Selector[7]);
  not not_841 (not_841_out, Selector[8]);
  not not_842 (not_842_out, Selector[9]);
  not not_843 (not_843_out, Selector[10]);
  not not_844 (not_844_out, Selector[11]);
  not not_845 (not_845_out, Selector[12]);
  not not_846 (not_846_out, Selector[13]);
  not not_847 (not_847_out, Selector[14]);
  not not_848 (not_848_out, Selector[15]);
  not not_849 (not_849_out, Selector[16]);
  not not_850 (not_850_out, Selector[17]);
  not not_851 (not_851_out, Selector[18]);
  not not_852 (not_852_out, Selector[19]);
  not not_853 (not_853_out, Selector[20]);
  not not_854 (not_854_out, Selector[21]);
  not not_855 (not_855_out, Selector[22]);
  not not_856 (not_856_out, Selector[23]);
  not not_857 (not_857_out, Selector[24]);
  not not_858 (not_858_out, Selector[25]);
  // NOT_Gate not_859 has open pins: in=Selector[26], out=open
  not not_860 (not_860_out, Selector[27]);
  not not_861 (not_861_out, Selector[28]);
  not not_862 (not_862_out, Selector[29]);
  not not_863 (not_863_out, Selector[30]);
  not not_864 (not_864_out, Selector[31]);
  not not_865 (not_865_out, Selector[0]);
  not not_866 (not_866_out, Selector[1]);
  not not_867 (not_867_out, Selector[2]);
  not not_868 (not_868_out, Selector[3]);
  not not_869 (not_869_out, Selector[4]);
  not not_870 (not_870_out, Selector[5]);
  not not_871 (not_871_out, Selector[6]);
  not not_872 (not_872_out, Selector[7]);
  not not_873 (not_873_out, Selector[8]);
  not not_874 (not_874_out, Selector[9]);
  not not_875 (not_875_out, Selector[10]);
  not not_876 (not_876_out, Selector[11]);
  not not_877 (not_877_out, Selector[12]);
  not not_878 (not_878_out, Selector[13]);
  not not_879 (not_879_out, Selector[14]);
  not not_880 (not_880_out, Selector[15]);
  not not_881 (not_881_out, Selector[16]);
  not not_882 (not_882_out, Selector[17]);
  not not_883 (not_883_out, Selector[18]);
  not not_884 (not_884_out, Selector[19]);
  not not_885 (not_885_out, Selector[20]);
  not not_886 (not_886_out, Selector[21]);
  not not_887 (not_887_out, Selector[22]);
  not not_888 (not_888_out, Selector[23]);
  not not_889 (not_889_out, Selector[24]);
  not not_890 (not_890_out, Selector[25]);
  not not_891 (not_891_out, Selector[26]);
  // NOT_Gate not_892 has open pins: in=Selector[27], out=open
  not not_893 (not_893_out, Selector[28]);
  not not_894 (not_894_out, Selector[29]);
  not not_895 (not_895_out, Selector[30]);
  not not_896 (not_896_out, Selector[31]);
  not not_897 (not_897_out, Selector[0]);
  not not_898 (not_898_out, Selector[1]);
  not not_899 (not_899_out, Selector[2]);
  not not_900 (not_900_out, Selector[3]);
  not not_901 (not_901_out, Selector[4]);
  not not_902 (not_902_out, Selector[5]);
  not not_903 (not_903_out, Selector[6]);
  not not_904 (not_904_out, Selector[7]);
  not not_905 (not_905_out, Selector[8]);
  not not_906 (not_906_out, Selector[9]);
  not not_907 (not_907_out, Selector[10]);
  not not_908 (not_908_out, Selector[11]);
  not not_909 (not_909_out, Selector[12]);
  not not_910 (not_910_out, Selector[13]);
  not not_911 (not_911_out, Selector[14]);
  not not_912 (not_912_out, Selector[15]);
  not not_913 (not_913_out, Selector[16]);
  not not_914 (not_914_out, Selector[17]);
  not not_915 (not_915_out, Selector[18]);
  not not_916 (not_916_out, Selector[19]);
  not not_917 (not_917_out, Selector[20]);
  not not_918 (not_918_out, Selector[21]);
  not not_919 (not_919_out, Selector[22]);
  not not_920 (not_920_out, Selector[23]);
  not not_921 (not_921_out, Selector[24]);
  not not_922 (not_922_out, Selector[25]);
  not not_923 (not_923_out, Selector[26]);
  not not_924 (not_924_out, Selector[27]);
  // NOT_Gate not_925 has open pins: in=Selector[28], out=open
  not not_926 (not_926_out, Selector[29]);
  not not_927 (not_927_out, Selector[30]);
  not not_928 (not_928_out, Selector[31]);
  not not_929 (not_929_out, Selector[0]);
  not not_930 (not_930_out, Selector[1]);
  not not_931 (not_931_out, Selector[2]);
  not not_932 (not_932_out, Selector[3]);
  not not_933 (not_933_out, Selector[4]);
  not not_934 (not_934_out, Selector[5]);
  not not_935 (not_935_out, Selector[6]);
  not not_936 (not_936_out, Selector[7]);
  not not_937 (not_937_out, Selector[8]);
  not not_938 (not_938_out, Selector[9]);
  not not_939 (not_939_out, Selector[10]);
  not not_940 (not_940_out, Selector[11]);
  not not_941 (not_941_out, Selector[12]);
  not not_942 (not_942_out, Selector[13]);
  not not_943 (not_943_out, Selector[14]);
  not not_944 (not_944_out, Selector[15]);
  not not_945 (not_945_out, Selector[16]);
  not not_946 (not_946_out, Selector[17]);
  not not_947 (not_947_out, Selector[18]);
  not not_948 (not_948_out, Selector[19]);
  not not_949 (not_949_out, Selector[20]);
  not not_950 (not_950_out, Selector[21]);
  not not_951 (not_951_out, Selector[22]);
  not not_952 (not_952_out, Selector[23]);
  not not_953 (not_953_out, Selector[24]);
  not not_954 (not_954_out, Selector[25]);
  not not_955 (not_955_out, Selector[26]);
  not not_956 (not_956_out, Selector[27]);
  not not_957 (not_957_out, Selector[28]);
  // NOT_Gate not_958 has open pins: in=Selector[29], out=open
  not not_959 (not_959_out, Selector[30]);
  not not_960 (not_960_out, Selector[31]);
  not not_961 (not_961_out, Selector[0]);
  not not_962 (not_962_out, Selector[1]);
  not not_963 (not_963_out, Selector[2]);
  not not_964 (not_964_out, Selector[3]);
  not not_965 (not_965_out, Selector[4]);
  not not_966 (not_966_out, Selector[5]);
  not not_967 (not_967_out, Selector[6]);
  not not_968 (not_968_out, Selector[7]);
  not not_969 (not_969_out, Selector[8]);
  not not_970 (not_970_out, Selector[9]);
  not not_971 (not_971_out, Selector[10]);
  not not_972 (not_972_out, Selector[11]);
  not not_973 (not_973_out, Selector[12]);
  not not_974 (not_974_out, Selector[13]);
  not not_975 (not_975_out, Selector[14]);
  not not_976 (not_976_out, Selector[15]);
  not not_977 (not_977_out, Selector[16]);
  not not_978 (not_978_out, Selector[17]);
  not not_979 (not_979_out, Selector[18]);
  not not_980 (not_980_out, Selector[19]);
  not not_981 (not_981_out, Selector[20]);
  not not_982 (not_982_out, Selector[21]);
  not not_983 (not_983_out, Selector[22]);
  not not_984 (not_984_out, Selector[23]);
  not not_985 (not_985_out, Selector[24]);
  not not_986 (not_986_out, Selector[25]);
  not not_987 (not_987_out, Selector[26]);
  not not_988 (not_988_out, Selector[27]);
  not not_989 (not_989_out, Selector[28]);
  not not_990 (not_990_out, Selector[29]);
  // NOT_Gate not_991 has open pins: in=Selector[30], out=open
  not not_992 (not_992_out, Selector[31]);
  not not_993 (not_993_out, Selector[0]);
  not not_994 (not_994_out, Selector[1]);
  not not_995 (not_995_out, Selector[2]);
  not not_996 (not_996_out, Selector[3]);
  not not_997 (not_997_out, Selector[4]);
  not not_998 (not_998_out, Selector[5]);
  not not_999 (not_999_out, Selector[6]);
  not not_1000 (not_1000_out, Selector[7]);
  not not_1001 (not_1001_out, Selector[8]);
  not not_1002 (not_1002_out, Selector[9]);
  not not_1003 (not_1003_out, Selector[10]);
  not not_1004 (not_1004_out, Selector[11]);
  not not_1005 (not_1005_out, Selector[12]);
  not not_1006 (not_1006_out, Selector[13]);
  not not_1007 (not_1007_out, Selector[14]);
  not not_1008 (not_1008_out, Selector[15]);
  not not_1009 (not_1009_out, Selector[16]);
  not not_1010 (not_1010_out, Selector[17]);
  not not_1011 (not_1011_out, Selector[18]);
  not not_1012 (not_1012_out, Selector[19]);
  not not_1013 (not_1013_out, Selector[20]);
  not not_1014 (not_1014_out, Selector[21]);
  not not_1015 (not_1015_out, Selector[22]);
  not not_1016 (not_1016_out, Selector[23]);
  not not_1017 (not_1017_out, Selector[24]);
  not not_1018 (not_1018_out, Selector[25]);
  not not_1019 (not_1019_out, Selector[26]);
  not not_1020 (not_1020_out, Selector[27]);
  not not_1021 (not_1021_out, Selector[28]);
  not not_1022 (not_1022_out, Selector[29]);
  not not_1023 (not_1023_out, Selector[30]);
  // NOT_Gate not_1024 has open pins: in=Selector[31], out=open
  and and_1 (and_1_out[31], not_2_out, not_3_out, not_4_out, not_5_out, not_6_out, not_7_out, not_8_out, not_9_out, not_10_out, not_11_out, not_12_out, not_13_out, not_14_out, not_15_out, not_16_out, not_17_out, not_19_out, not_20_out, not_21_out, not_22_out, not_23_out, not_24_out, not_25_out, not_26_out, not_27_out, not_28_out, not_29_out, not_30_out, not_31_out, not_32_out, Selector[0], not_18_out);
  and and_2 (and_2_out[31], not_33_out, not_35_out, not_36_out, not_37_out, not_38_out, not_39_out, not_40_out, not_41_out, not_42_out, not_43_out, not_44_out, not_45_out, not_46_out, not_47_out, not_48_out, not_49_out, not_51_out, not_52_out, not_53_out, not_54_out, not_55_out, not_56_out, not_57_out, not_58_out, not_59_out, not_60_out, not_61_out, not_62_out, not_63_out, not_64_out, Selector[1], not_50_out);
  and and_3 (and_3_out[31], not_65_out, not_66_out, not_68_out, not_69_out, not_70_out, not_71_out, not_72_out, not_73_out, not_74_out, not_75_out, not_76_out, not_77_out, not_78_out, not_79_out, not_80_out, not_81_out, not_83_out, not_84_out, not_85_out, not_86_out, not_87_out, not_88_out, not_89_out, not_90_out, not_91_out, not_92_out, not_93_out, not_94_out, not_95_out, not_96_out, Selector[2], not_82_out);
  and and_4 (and_4_out[31], not_97_out, not_98_out, not_99_out, not_101_out, not_102_out, not_103_out, not_104_out, not_105_out, not_106_out, not_107_out, not_108_out, not_109_out, not_110_out, not_111_out, not_112_out, not_113_out, not_115_out, not_116_out, not_117_out, not_118_out, not_119_out, not_120_out, not_121_out, not_122_out, not_123_out, not_124_out, not_125_out, not_126_out, not_127_out, not_128_out, Selector[3], not_114_out);
  and and_5 (and_5_out[31], not_129_out, not_130_out, not_131_out, not_132_out, not_134_out, not_135_out, not_136_out, not_137_out, not_138_out, not_139_out, not_140_out, not_141_out, not_142_out, not_143_out, not_144_out, not_145_out, not_147_out, not_148_out, not_149_out, not_150_out, not_151_out, not_152_out, not_153_out, not_154_out, not_155_out, not_156_out, not_157_out, not_158_out, not_159_out, not_160_out, Selector[4], not_146_out);
  and and_6 (and_6_out[31], not_161_out, not_162_out, not_164_out, not_163_out, not_166_out, not_167_out, not_168_out, not_169_out, not_170_out, not_171_out, not_172_out, not_173_out, not_174_out, not_175_out, not_176_out, not_177_out, not_179_out, not_180_out, not_181_out, not_182_out, not_183_out, not_184_out, not_185_out, not_186_out, not_187_out, not_188_out, not_189_out, not_190_out, not_191_out, not_192_out, Selector[5], not_178_out);
  and and_7 (and_7_out[31], not_193_out, not_194_out, not_196_out, not_197_out, not_198_out, not_195_out, not_200_out, not_201_out, not_202_out, not_203_out, not_204_out, not_205_out, not_206_out, not_207_out, not_208_out, not_209_out, not_211_out, not_212_out, not_213_out, not_214_out, not_215_out, not_216_out, not_217_out, not_218_out, not_219_out, not_220_out, not_221_out, not_222_out, not_223_out, not_224_out, Selector[6], not_210_out);
  and and_8 (and_8_out[31], not_225_out, not_226_out, not_228_out, not_229_out, not_230_out, not_231_out, not_227_out, not_233_out, not_234_out, not_235_out, not_236_out, not_237_out, not_238_out, not_239_out, not_240_out, not_241_out, not_243_out, not_244_out, not_245_out, not_246_out, not_247_out, not_248_out, not_249_out, not_250_out, not_251_out, not_252_out, not_253_out, not_254_out, not_255_out, not_256_out, Selector[7], not_242_out);
  and and_9 (and_9_out[31], not_258_out, not_259_out, not_260_out, not_261_out, not_262_out, not_263_out, not_264_out, not_257_out, not_266_out, not_267_out, not_268_out, not_269_out, not_270_out, not_271_out, not_272_out, not_273_out, not_275_out, not_276_out, not_277_out, not_278_out, not_279_out, not_280_out, not_281_out, not_282_out, not_283_out, not_284_out, not_285_out, not_286_out, not_287_out, not_288_out, Selector[8], not_274_out);
  and and_10 (and_10_out[31], not_289_out, not_291_out, not_292_out, not_293_out, not_294_out, not_295_out, not_296_out, not_297_out, not_290_out, not_299_out, not_300_out, not_301_out, not_302_out, not_303_out, not_304_out, not_305_out, not_307_out, not_308_out, not_309_out, not_310_out, not_311_out, not_312_out, not_313_out, not_314_out, not_315_out, not_316_out, not_317_out, not_318_out, not_319_out, not_320_out, Selector[9], not_306_out);
  and and_11 (and_11_out[31], not_321_out, not_322_out, not_324_out, not_325_out, not_326_out, not_327_out, not_328_out, not_329_out, not_330_out, not_323_out, not_332_out, not_333_out, not_334_out, not_335_out, not_336_out, not_337_out, not_339_out, not_340_out, not_341_out, not_342_out, not_343_out, not_344_out, not_345_out, not_346_out, not_347_out, not_348_out, not_349_out, not_350_out, not_351_out, not_352_out, Selector[10], not_338_out);
  and and_12 (and_12_out[31], not_353_out, not_354_out, not_356_out, not_357_out, not_358_out, not_359_out, not_360_out, not_361_out, not_362_out, not_363_out, not_355_out, not_365_out, not_366_out, not_367_out, not_368_out, not_369_out, not_371_out, not_372_out, not_373_out, not_374_out, not_375_out, not_376_out, not_377_out, not_378_out, not_379_out, not_380_out, not_381_out, not_382_out, not_383_out, not_384_out, Selector[11], not_370_out);
  and and_13 (and_13_out[31], not_385_out, not_386_out, not_388_out, not_389_out, not_390_out, not_391_out, not_392_out, not_393_out, not_394_out, not_395_out, not_396_out, not_387_out, not_398_out, not_399_out, not_400_out, not_401_out, not_403_out, not_404_out, not_405_out, not_406_out, not_407_out, not_408_out, not_409_out, not_410_out, not_411_out, not_412_out, not_413_out, not_414_out, not_415_out, not_416_out, Selector[12], not_402_out);
  and and_14 (and_14_out[31], not_417_out, not_418_out, not_420_out, not_421_out, not_422_out, not_423_out, not_424_out, not_425_out, not_426_out, not_427_out, not_428_out, not_429_out, not_419_out, not_431_out, not_432_out, not_433_out, not_435_out, not_436_out, not_437_out, not_438_out, not_439_out, not_440_out, not_441_out, not_442_out, not_443_out, not_444_out, not_445_out, not_446_out, not_447_out, not_448_out, Selector[13], not_434_out);
  and and_15 (and_15_out[31], not_449_out, not_450_out, not_452_out, not_453_out, not_454_out, not_455_out, not_456_out, not_457_out, not_458_out, not_459_out, not_460_out, not_461_out, not_462_out, not_451_out, not_464_out, not_465_out, not_467_out, not_468_out, not_469_out, not_470_out, not_471_out, not_472_out, not_473_out, not_474_out, not_475_out, not_476_out, not_477_out, not_478_out, not_479_out, not_480_out, Selector[14], not_466_out);
  and and_16 (and_16_out[31], not_481_out, not_482_out, not_484_out, not_485_out, not_486_out, not_487_out, not_488_out, not_489_out, not_490_out, not_491_out, not_492_out, not_493_out, not_494_out, not_495_out, not_483_out, not_497_out, not_499_out, not_500_out, not_501_out, not_502_out, not_503_out, not_504_out, not_505_out, not_506_out, not_507_out, not_508_out, not_509_out, not_510_out, not_511_out, not_512_out, Selector[15], not_498_out);
  and and_17 (and_17_out[31], not_514_out, not_515_out, not_516_out, not_517_out, not_518_out, not_519_out, not_520_out, not_521_out, not_522_out, not_523_out, not_524_out, not_525_out, not_526_out, not_527_out, not_528_out, not_513_out, not_531_out, not_532_out, not_533_out, not_534_out, not_535_out, not_536_out, not_537_out, not_538_out, not_539_out, not_540_out, not_541_out, not_542_out, not_543_out, not_544_out, Selector[16], not_530_out);
  and and_18 (and_18_out[31], not_545_out, not_547_out, not_548_out, not_549_out, not_550_out, not_551_out, not_552_out, not_553_out, not_554_out, not_555_out, not_556_out, not_557_out, not_558_out, not_559_out, not_560_out, not_561_out, not_563_out, not_564_out, not_565_out, not_566_out, not_567_out, not_568_out, not_569_out, not_570_out, not_571_out, not_572_out, not_573_out, not_574_out, not_575_out, not_576_out, Selector[17], not_546_out);
  and and_19 (and_19_out[31], not_577_out, not_578_out, not_580_out, not_581_out, not_582_out, not_583_out, not_584_out, not_585_out, not_586_out, not_587_out, not_588_out, not_589_out, not_590_out, not_591_out, not_592_out, not_593_out, not_579_out, not_596_out, not_597_out, not_598_out, not_599_out, not_600_out, not_601_out, not_602_out, not_603_out, not_604_out, not_605_out, not_606_out, not_607_out, not_608_out, Selector[18], not_594_out);
  and and_20 (and_20_out[31], not_609_out, not_610_out, not_612_out, not_613_out, not_614_out, not_615_out, not_616_out, not_617_out, not_618_out, not_619_out, not_620_out, not_621_out, not_622_out, not_623_out, not_624_out, not_625_out, not_627_out, not_611_out, not_629_out, not_630_out, not_631_out, not_632_out, not_633_out, not_634_out, not_635_out, not_636_out, not_637_out, not_638_out, not_639_out, not_640_out, Selector[19], not_626_out);
  and and_21 (and_21_out[31], not_641_out, not_642_out, not_644_out, not_645_out, not_646_out, not_647_out, not_648_out, not_649_out, not_650_out, not_651_out, not_652_out, not_653_out, not_654_out, not_655_out, not_656_out, not_657_out, not_659_out, not_660_out, not_643_out, not_662_out, not_663_out, not_664_out, not_665_out, not_666_out, not_667_out, not_668_out, not_669_out, not_670_out, not_671_out, not_672_out, Selector[20], not_658_out);
  and and_22 (and_22_out[31], not_673_out, not_674_out, not_676_out, not_677_out, not_678_out, not_679_out, not_680_out, not_681_out, not_682_out, not_683_out, not_684_out, not_685_out, not_686_out, not_687_out, not_688_out, not_689_out, not_691_out, not_692_out, not_693_out, not_675_out, not_695_out, not_696_out, not_697_out, not_698_out, not_699_out, not_700_out, not_701_out, not_702_out, not_703_out, not_704_out, Selector[21], not_690_out);
  and and_23 (and_23_out[31], not_705_out, not_706_out, not_708_out, not_709_out, not_710_out, not_711_out, not_712_out, not_713_out, not_714_out, not_715_out, not_716_out, not_717_out, not_718_out, not_719_out, not_720_out, not_721_out, not_723_out, not_724_out, not_725_out, not_726_out, not_707_out, not_728_out, not_729_out, not_730_out, not_731_out, not_732_out, not_733_out, not_734_out, not_735_out, not_736_out, Selector[22], not_722_out);
  and and_24 (and_24_out[31], not_737_out, not_738_out, not_740_out, not_741_out, not_742_out, not_743_out, not_744_out, not_745_out, not_746_out, not_747_out, not_748_out, not_749_out, not_750_out, not_751_out, not_752_out, not_753_out, not_755_out, not_756_out, not_757_out, not_758_out, not_759_out, not_739_out, not_761_out, not_762_out, not_763_out, not_764_out, not_765_out, not_766_out, not_767_out, not_768_out, Selector[23], not_754_out);
  and and_25 (and_25_out[31], not_770_out, not_771_out, not_772_out, not_773_out, not_774_out, not_775_out, not_776_out, not_777_out, not_778_out, not_779_out, not_780_out, not_781_out, not_782_out, not_783_out, not_784_out, not_785_out, not_787_out, not_788_out, not_789_out, not_790_out, not_791_out, not_792_out, not_769_out, not_794_out, not_795_out, not_796_out, not_797_out, not_798_out, not_799_out, not_800_out, Selector[24], not_786_out);
  and and_26 (and_26_out[31], not_801_out, not_803_out, not_804_out, not_805_out, not_806_out, not_807_out, not_808_out, not_809_out, not_810_out, not_811_out, not_812_out, not_813_out, not_814_out, not_815_out, not_816_out, not_817_out, not_819_out, not_820_out, not_821_out, not_822_out, not_823_out, not_824_out, not_825_out, not_802_out, not_827_out, not_828_out, not_829_out, not_830_out, not_831_out, not_832_out, Selector[25], not_818_out);
  and and_27 (and_27_out[31], not_833_out, not_834_out, not_836_out, not_837_out, not_838_out, not_839_out, not_840_out, not_841_out, not_842_out, not_843_out, not_844_out, not_845_out, not_846_out, not_847_out, not_848_out, not_849_out, not_851_out, not_852_out, not_853_out, not_854_out, not_855_out, not_856_out, not_857_out, not_858_out, not_835_out, not_860_out, not_861_out, not_862_out, not_863_out, not_864_out, Selector[26], not_850_out);
  and and_28 (and_28_out[31], not_865_out, not_866_out, not_868_out, not_869_out, not_870_out, not_871_out, not_872_out, not_873_out, not_874_out, not_875_out, not_876_out, not_877_out, not_878_out, not_879_out, not_880_out, not_881_out, not_883_out, not_884_out, not_885_out, not_886_out, not_887_out, not_888_out, not_889_out, not_890_out, not_891_out, not_867_out, not_893_out, not_894_out, not_895_out, not_896_out, Selector[27], not_882_out);
  and and_29 (and_29_out[31], not_897_out, not_898_out, not_900_out, not_901_out, not_902_out, not_903_out, not_904_out, not_905_out, not_906_out, not_907_out, not_908_out, not_909_out, not_910_out, not_911_out, not_912_out, not_913_out, not_915_out, not_916_out, not_917_out, not_918_out, not_919_out, not_920_out, not_921_out, not_922_out, not_923_out, not_924_out, not_899_out, not_926_out, not_927_out, not_928_out, Selector[28], not_914_out);
  and and_30 (and_30_out[31], not_929_out, not_930_out, not_932_out, not_933_out, not_934_out, not_935_out, not_936_out, not_937_out, not_938_out, not_939_out, not_940_out, not_941_out, not_942_out, not_943_out, not_944_out, not_945_out, not_947_out, not_948_out, not_949_out, not_950_out, not_951_out, not_952_out, not_953_out, not_954_out, not_955_out, not_956_out, not_957_out, not_931_out, not_959_out, not_960_out, Selector[29], not_946_out);
  and and_31 (and_31_out[31], not_961_out, not_962_out, not_964_out, not_965_out, not_966_out, not_967_out, not_968_out, not_969_out, not_970_out, not_971_out, not_972_out, not_973_out, not_974_out, not_975_out, not_976_out, not_977_out, not_979_out, not_980_out, not_981_out, not_982_out, not_983_out, not_984_out, not_985_out, not_986_out, not_987_out, not_988_out, not_989_out, not_990_out, not_963_out, not_992_out, Selector[30], not_978_out);
  and and_32 (and_32_out[31], not_993_out, not_994_out, not_996_out, not_997_out, not_998_out, not_999_out, not_1000_out, not_1001_out, not_1002_out, not_1003_out, not_1004_out, not_1005_out, not_1006_out, not_1007_out, not_1008_out, not_1009_out, not_1011_out, not_1012_out, not_1013_out, not_1014_out, not_1015_out, not_1016_out, not_1017_out, not_1018_out, not_1019_out, not_1020_out, not_1021_out, not_1022_out, not_1023_out, not_995_out, Selector[31], not_1010_out);
  assign and_33_out = Data_Input_0 & {32{and_1_out[31]}};  // AND_Gate and_33, 32 bits wide
  assign Output = and_33_out | or_27_out;  // OR_Gate or_1, 32 bits wide
  assign and_34_out = Data_Input_1 & {32{and_2_out[31]}};  // AND_Gate and_34, 32 bits wide
  assign and_35_out = Data_Input_2 & {32{and_3_out[31]}};  // AND_Gate and_35, 32 bits wide
  assign and_36_out = Data_Input_3 & {32{and_4_out[31]}};  // AND_Gate and_36, 32 bits wide
  assign and_37_out = Data_Input_4 & {32{and_5_out[31]}};  // AND_Gate and_37, 32 bits wide
  assign and_38_out = Data_Input_5 & {32{and_6_out[31]}};  // AND_Gate and_38, 32 bits wide
  assign and_39_out = Data_Input_6 & {32{and_7_out[31]}};  // AND_Gate and_39, 32 bits wide
  assign and_40_out = Data_Input_7 & {32{and_8_out[31]}};  // AND_Gate and_40, 32 bits wide
  assign and_41_out = Data_Input_8 & {32{and_9_out[31]}};  // AND_Gate and_41, 32 bits wide
  assign and_42_out = Data_Input_9 & {32{and_10_out[31]}};  // AND_Gate and_42, 32 bits wide
  assign and_43_out = Data_Input_10 & {32{and_11_out[31]}};  // AND_Gate and_43, 32 bits wide
  assign and_44_out = Data_Input_11 & {32{and_12_out[31]}};  // AND_Gate and_44, 32 bits wide
  assign and_45_out = Data_Input_12 & {32{and_13_out[31]}};  // AND_Gate and_45, 32 bits wide
  assign and_46_out = Data_Input_13 & {32{and_14_out[31]}};  // AND_Gate and_46, 32 bits wide
  assign and_47_out = Data_Input_14 & {32{and_15_out[31]}};  // AND_Gate and_47, 32 bits wide
  assign and_48_out = Data_Input_15 & {32{and_16_out[31]}};  // AND_Gate and_48, 32 bits wide
  assign and_49_out = Data_Input_16 & {32{and_17_out[31]}};  // AND_Gate and_49, 32 bits wide
  assign and_50_out = Data_Input_17 & {32{and_18_out[31]}};  // AND_Gate and_50, 32 bits wide
  assign and_51_out = Data_Input_18 & {32{and_19_out[31]}};  // AND_Gate and_51, 32 bits wide
  assign and_52_out = Data_Input_19 & {32{and_20_out[31]}};  // AND_Gate and_52, 32 bits wide
  assign and_53_out = Data_Input_20 & {32{and_21_out[31]}};  // AND_Gate and_53, 32 bits wide
  assign and_54_out = Data_Input_21 & {32{and_22_out[31]}};  // AND_Gate and_54, 32 bits wide
  assign and_55_out = Data_Input_22 & {32{and_23_out[31]}};  // AND_Gate and_55, 32 bits wide
  assign and_56_out = Data_Input_23 & {32{and_24_out[31]}};  // AND_Gate and_56, 32 bits wide
  assign and_57_out = Data_Input_24 & {32{and_25_out[31]}};  // AND_Gate and_57, 32 bits wide
  assign and_58_out = Data_Input_25 & {32{and_26_out[31]}};  // AND_Gate and_58, 32 bits wide
  assign and_59_out = Data_Input_26 & {32{and_27_out[31]}};  // AND_Gate and_59, 32 bits wide
  assign and_60_out = Data_Input_27 & {32{and_28_out[31]}};  // AND_Gate and_60, 32 bits wide
  assign and_61_out = Data_Input_28 & {32{and_29_out[31]}};  // AND_Gate and_61, 32 bits wide
  assign and_62_out = Data_Input_29 & {32{and_30_out[31]}};  // AND_Gate and_62, 32 bits wide
  assign and_63_out = Data_Input_30 & {32{and_31_out[31]}};  // AND_Gate and_63, 32 bits wide
  assign and_64_out = Data_Input_31 & {32{and_32_out[31]}};  // AND_Gate and_64, 32 bits wide
  assign or_2_out = and_44_out | or_3_out;  // OR_Gate or_2, 32 bits wide
  assign or_3_out = and_45_out | or_30_out;  // OR_Gate or_3, 32 bits wide
  assign or_4_out = and_54_out | or_31_out;  // OR_Gate or_4, 32 bits wide
  assign or_5_out = and_43_out | or_2_out;  // OR_Gate or_5, 32 bits wide
  assign or_6_out = and_52_out | or_7_out;  // OR_Gate or_6, 32 bits wide
  assign or_7_out = and_53_out | or_4_out;  // OR_Gate or_7, 32 bits wide
  assign or_8_out = and_62_out | or_9_out;  // OR_Gate or_8, 32 bits wide
  assign or_9_out = and_63_out | and_64_out;  // OR_Gate or_9, 32 bits wide
  assign or_10_out = and_42_out | or_5_out;  // OR_Gate or_10, 32 bits wide
  assign or_11_out = and_51_out | or_6_out;  // OR_Gate or_11, 32 bits wide
  assign or_12_out = and_61_out | or_8_out;  // OR_Gate or_12, 32 bits wide
  assign or_13_out = and_41_out | or_10_out;  // OR_Gate or_13, 32 bits wide
  assign or_14_out = and_50_out | or_11_out;  // OR_Gate or_14, 32 bits wide
  assign or_15_out = and_60_out | or_12_out;  // OR_Gate or_15, 32 bits wide
  assign or_16_out = and_38_out | or_17_out;  // OR_Gate or_16, 32 bits wide
  assign or_17_out = and_39_out | or_18_out;  // OR_Gate or_17, 32 bits wide
  assign or_18_out = and_40_out | or_13_out;  // OR_Gate or_18, 32 bits wide
  assign or_19_out = and_49_out | or_14_out;  // OR_Gate or_19, 32 bits wide
  assign or_20_out = and_59_out | or_15_out;  // OR_Gate or_20, 32 bits wide
  assign or_21_out = and_37_out | or_16_out;  // OR_Gate or_21, 32 bits wide
  assign or_22_out = and_48_out | or_19_out;  // OR_Gate or_22, 32 bits wide
  assign or_23_out = and_58_out | or_20_out;  // OR_Gate or_23, 32 bits wide
  assign or_24_out = and_35_out | or_25_out;  // OR_Gate or_24, 32 bits wide
  assign or_25_out = and_36_out | or_21_out;  // OR_Gate or_25, 32 bits wide
  assign or_26_out = and_57_out | or_23_out;  // OR_Gate or_26, 32 bits wide
  assign or_27_out = and_34_out | or_24_out;  // OR_Gate or_27, 32 bits wide
  assign or_28_out = and_47_out | or_22_out;  // OR_Gate or_28, 32 bits wide
  assign or_29_out = and_56_out | or_26_out;  // OR_Gate or_29, 32 bits wide
  assign or_30_out = and_46_out | or_28_out;  // OR_Gate or_30, 32 bits wide
  assign or_31_out = and_55_out | or_29_out;  // OR_Gate or_31, 32 bits wide
endmodule
module Register_File_x2 (
  input  Clock,
  input  [31:0] Data_Input,
  input  [4:0] SA,
  input  RW,
  input  Rst,
  input  [4:0] DA,
  input  [4:0] SB,
  input  [31:0] HI_Input,
  input  [31:0] LO_Input,
  input  HI___LO_enable,
  output [31:0] A,
  output [31:0] B,
  output [31:0] Hi_value,
  output [31:0] Lo_Value
);

  wire decoder_1_out1, decoder_1_out2, decoder_1_out3, decoder_1_out4, decoder_1_out5, decoder_1_out6,
       decoder_1_out7, decoder_1_out8, decoder_1_out9, decoder_1_out10, decoder_1_out11, decoder_1_out12,
       decoder_1_out13, decoder_1_out14, decoder_1_out15, not_1_out, not_2_out;
  wire [15:0] decoder_1_out16;
  wire [31:0] register_1_q, register_2_q, register_3_q, register_4_q, register_5_q, register_6_q,
       register_7_q, register_8_q, register_9_q, register_10_q, register_11_q, register_12_q, register_13_q,
       register_14_q, register_15_q, register_16_q, register_17_q, register_18_q, register_19_q,
       register_20_q, register_21_q, register_22_q, register_23_q, register_24_q, register_25_q,
       register_26_q, register_27_q, register_28_q, register_29_q, register_30_q, register_31_q,
       register_32_q;

  not not_1 (not_1_out, 1'b1);
  Decoder #(.select(5)) decoder_1 (
    .out1(decoder_1_out1), .out2(decoder_1_out2), .out3(decoder_1_out3), .out4(decoder_1_out4),
    .out5(decoder_1_out5), .out6(decoder_1_out6), .out7(decoder_1_out7), .out8(decoder_1_out8),
    .out9(decoder_1_out9), .out10(decoder_1_out10), .out11(decoder_1_out11), .out12(decoder_1_out12),
    .out13(decoder_1_out13), .out14(decoder_1_out14), .out15(decoder_1_out15), .out16(decoder_1_out16[0]),
    .out17(decoder_1_out16[1]), .out18(decoder_1_out16[2]), .out19(decoder_1_out16[3]),
    .out20(decoder_1_out16[4]), .out21(decoder_1_out16[5]), .out22(decoder_1_out16[6]),
    .out23(decoder_1_out16[7]), .out24(decoder_1_out16[8]), .out25(decoder_1_out16[9]),
    .out26(decoder_1_out16[10]), .out27(decoder_1_out16[11]), .out28(decoder_1_out16[12]),
    .out29(decoder_1_out16[13]), .out30(decoder_1_out16[14]), .out31(decoder_1_out16[15]), .sel(DA), .en(RW));  // open: out0
  Register #(.width(32)) register_1 (.D(Data_Input), .en(not_1_out), .Q(register_1_q), .clk(Clock), .clr(not_2_out));
  Register #(.width(32)) register_2 (.D(Data_Input), .en(decoder_1_out1), .Q(register_2_q), .clk(Clock), .clr(Rst));
  Register #(.width(32)) register_3 (.D(Data_Input), .en(decoder_1_out2), .Q(register_3_q), .clk(Clock), .clr(Rst));
  Register #(.width(32)) register_4 (.D(Data_Input), .en(decoder_1_out3), .Q(register_4_q), .clk(Clock), .clr(Rst));
  Register #(.width(32)) register_5 (.D(Data_Input), .en(decoder_1_out4), .Q(register_5_q), .clk(Clock), .clr(Rst));
  Register #(.width(32)) register_6 (.D(Data_Input), .en(decoder_1_out6), .Q(register_6_q), .clk(Clock), .clr(Rst));
  Register #(.width(32)) register_7 (.D(Data_Input), .en(decoder_1_out7), .Q(register_7_q), .clk(Clock), .clr(Rst));
  Register #(.width(32)) register_8 (.D(Data_Input), .en(decoder_1_out8), .Q(register_8_q), .clk(Clock), .clr(Rst));
  Register #(.width(32)) register_9 (.D(Data_Input), .en(decoder_1_out5), .Q(register_9_q), .clk(Clock), .clr(Rst));
  Register #(.width(32)) register_10 (.D(Data_Input), .en(decoder_1_out9), .Q(register_10_q), .clk(Clock), .clr(Rst));
  Register #(.width(32)) register_11 (.D(Data_Input), .en(decoder_1_out10), .Q(register_11_q), .clk(Clock), .clr(Rst));
  Register #(.width(32)) register_12 (.D(Data_Input), .en(decoder_1_out11), .Q(register_12_q), .clk(Clock), .clr(Rst));
  Register #(.width(32)) register_13 (.D(Data_Input), .en(decoder_1_out12), .Q(register_13_q), .clk(Clock), .clr(Rst));
  Register #(.width(32)) register_14 (.D(Data_Input), .en(decoder_1_out13), .Q(register_14_q), .clk(Clock), .clr(Rst));
  Register #(.width(32)) register_15 (.D(Data_Input), .en(decoder_1_out14), .Q(register_15_q), .clk(Clock), .clr(Rst));
  Register #(.width(32)) register_16 (.D(Data_Input), .en(decoder_1_out15), .Q(register_16_q), .clk(Clock), .clr(Rst));
  Hi hi_1 (.Input(HI_Input), .Enable(HI___LO_enable), .Output(Hi_value), .Clock(Clock));
  Lo lo_1 (.Input(LO_Input), .Enable(HI___LO_enable), .Clock(Clock), .Output(Lo_Value));
  not not_2 (not_2_out, 1'b1);
  Register #(.width(32)) register_17 (
    .D(Data_Input), .en(decoder_1_out16[0]), .Q(register_17_q), .clk(Clock), .clr(Rst));
  Register #(.width(32)) register_18 (
    .D(Data_Input), .en(decoder_1_out16[1]), .Q(register_18_q), .clk(Clock), .clr(Rst));
  Register #(.width(32)) register_19 (
    .D(Data_Input), .en(decoder_1_out16[2]), .Q(register_19_q), .clk(Clock), .clr(Rst));
  Register #(.width(32)) register_20 (
    .D(Data_Input), .en(decoder_1_out16[3]), .Q(register_20_q), .clk(Clock), .clr(Rst));
  Register #(.width(32)) register_21 (
    .D(Data_Input), .en(decoder_1_out16[4]), .Q(register_21_q), .clk(Clock), .clr(Rst));
  Register #(.width(32)) register_22 (
    .D(Data_Input), .en(decoder_1_out16[5]), .Q(register_22_q), .clk(Clock), .clr(Rst));
  Register #(.width(32)) register_23 (
    .D(Data_Input), .en(decoder_1_out16[6]), .Q(register_23_q), .clk(Clock), .clr(Rst));
  Register #(.width(32)) register_24 (
    .D(Data_Input), .en(decoder_1_out16[7]), .Q(register_24_q), .clk(Clock), .clr(Rst));
  Register #(.width(32)) register_25 (
    .D(Data_Input), .en(decoder_1_out16[8]), .Q(register_25_q), .clk(Clock), .clr(Rst));
  Register #(.width(32)) register_26 (
    .D(Data_Input), .en(decoder_1_out16[9]), .Q(register_26_q), .clk(Clock), .clr(Rst));
  Register #(.width(32)) register_27 (
    .D(Data_Input), .en(decoder_1_out16[10]), .Q(register_27_q), .clk(Clock), .clr(Rst));
  Register #(.width(32)) register_28 (
    .D(Data_Input), .en(decoder_1_out16[11]), .Q(register_28_q), .clk(Clock), .clr(Rst));
  Register #(.width(32)) register_29 (
    .D(Data_Input), .en(decoder_1_out16[12]), .Q(register_29_q), .clk(Clock), .clr(Rst));
  Register #(.width(32)) register_30 (
    .D(Data_Input), .en(decoder_1_out16[13]), .Q(register_30_q), .clk(Clock), .clr(Rst));
  Register #(.width(32)) register_31 (
    .D(Data_Input), .en(decoder_1_out16[14]), .Q(register_31_q), .clk(Clock), .clr(Rst));
  Register #(.width(32)) register_32 (
    .D(Data_Input), .en(decoder_1_out16[15]), .Q(register_32_q), .clk(Clock), .clr(Rst));
  Multiplexer #(.select(5), .width(32)) multiplexer_1 (
    .in0(register_1_q), .in1(register_2_q), .in2(register_3_q), .in3(register_4_q), .in4(register_5_q),
    .in5(register_6_q), .in6(register_7_q), .in7(register_8_q), .in8(register_9_q), .in9(register_10_q),
    .in10(register_11_q), .in11(register_12_q), .in12(register_13_q), .in13(register_14_q),
    .in14(register_15_q), .in15(register_16_q), .in16(register_17_q), .in17(register_18_q),
    .in18(register_19_q), .in19(register_20_q), .in20(register_21_q), .in21(register_22_q),
    .in22(register_23_q), .in23(register_24_q), .in24(register_25_q), .in25(register_26_q),
    .in26(register_27_q), .in27(register_28_q), .in28(register_29_q), .in29(register_30_q),
    .in30(register_31_q), .in31(register_32_q), .out(A), .sel(SA));  // open: en
  Multiplexer #(.select(5), .width(32)) multiplexer_2 (
    .in0(register_1_q), .in1(register_2_q), .in2(register_3_q), .in3(register_4_q), .in4(register_5_q),
    .in5(register_6_q), .in6(register_7_q), .in7(register_8_q), .in8(register_9_q), .in9(register_10_q),
    .in10(register_11_q), .in11(register_12_q), .in12(register_13_q), .in13(register_14_q),
    .in14(register_15_q), .in15(register_16_q), .in16(register_17_q), .in17(register_18_q),
    .in18(register_19_q), .in19(register_20_q), .in20(register_21_q), .in21(register_22_q),
    .in22(register_23_q), .in23(register_24_q), .in24(register_25_q), .in25(register_26_q),
    .in26(register_27_q), .in27(register_28_q), .in28(register_29_q), .in29(register_30_q),
    .in30(register_31_q), .in31(register_32_q), .out(B), .sel(SB));  // open: en
endmodule

// ALU
module ALU_2_0 (
  input  [31:0] A,
  input  [31:0] B,
  input  [15:0] Constant,
  input  [31:0] Op,
  output [31:0] Output,
  output [31:0] Hi_Value,
  output [31:0] Lo_Value,
  output Hi___LO_was_used
);

  wire and_2_out, and_3_out, and_4_out, and_5_out;
  wire [0:0] c3;
  wire [1:0] MUX, not_3_out, not_4_out, not_5_out, not_6_out, O1, O2, O3, O4;
  wire [1:1] c2;
  wire [31:0] _0, _1, _2, _3, adder_1_out, adder_2_out, And_out, Andi_out, bit_extender_1_out, divider_1_out,
       multiplexer_5_out, multiplier_1_out, Nor_out, not_7_out, Or_out, Ori_out, slt_1_output, slti_1_output,
       sltiu_1_output, subtractor_1_out, unsigned_div_1_output, unsigned_mult_1_output,
       unsigned_slt_1_output, Xor_out, Xori_out;

  not not_1 (c2[1], 1'b1);
  not not_2 (c3[0], 1'b1);
  assign bit_extender_1_out = {{16{1'b0}}, Constant};  // Bit_Extender bit_extender_1
  Adder #(.width(32)) adder_1 (.a(A), .b(B), .out(adder_1_out));  // open: cin, cout
  Subtractor #(.width(32)) subtractor_1 (.a(A), .b(B), .out(subtractor_1_out));  // open: bin, bout
  Multiplier #(.width(32)) multiplier_1 (.a(A), .b(B), .out(multiplier_1_out), .cout(_0));  // open: cin
  Unsigned_Mult unsigned_mult_1 (.in_1(A), .in_2(B), .Output(unsigned_mult_1_output), .Output_2(_1));
  Divider #(.width(32)) divider_1 (.a(A), .b(B), .out(divider_1_out), .rem(_2));  // open: upper
  Unsigned_Div unsigned_div_1 (.in_1(A), .in_2(B), .Output(unsigned_div_1_output), .Output_2(_3));
  Adder #(.width(32)) adder_2 (.a(A), .b(bit_extender_1_out), .out(adder_2_out));  // open: cin, cout
  assign And_out = A & B;  // AND_Gate And, 32 bits wide
  assign Or_out = A | B;  // OR_Gate Or, 32 bits wide
  assign Nor_out = ~(A | B);  // NOR_Gate Nor, 32 bits wide
  assign Xor_out = A ^ B;  // XOR_Gate Xor, 32 bits wide
  assign Andi_out = A & bit_extender_1_out;  // AND_Gate Andi, 32 bits wide
  assign Ori_out = A | bit_extender_1_out;  // OR_Gate Ori, 32 bits wide
  assign Xori_out = A ^ bit_extender_1_out;  // XOR_Gate Xori, 32 bits wide
  Slt slt_1 (.Rs(A), .Rt(B), .Output(slt_1_output));
  Unsigned_Slt unsigned_slt_1 (.Rs(A), .Rt(B), .Output(unsigned_slt_1_output));
  Slti slti_1 (.Rs(A), .Constant(bit_extender_1_out), .Output(slti_1_output));
  Sltiu sltiu_1 (.Rs(A), .Constant(bit_extender_1_out), .Output(sltiu_1_output));
  assign not_3_out = ~2'b11;  // NOT_Gate not_3, 2 bits wide
  and and_2 (and_2_out, Op[2], ~Op[3], ~Op[4], ~Op[5]);  // AND_Gate
  assign not_4_out = ~2'b11;  // NOT_Gate not_4, 2 bits wide
  and and_3 (and_3_out, ~Op[2], Op[3], ~Op[4], ~Op[5]);  // AND_Gate
  assign not_5_out = ~2'b11;  // NOT_Gate not_5, 2 bits wide
  and and_4 (and_4_out, ~Op[2], ~Op[3], Op[4], ~Op[5]);  // AND_Gate
  assign not_6_out = ~2'b11;  // NOT_Gate not_6, 2 bits wide
  and and_5 (and_5_out, ~Op[2], ~Op[3], ~Op[4], Op[5]);  // AND_Gate
  Multiplexer #(.width(2)) multiplexer_1 (.in0(not_3_out), .in1(not_3_out), .out(O1), .sel(and_2_out));  // open: en
  Multiplexer #(.width(2)) multiplexer_2 (.in0(not_4_out), .in1({c2[1], 1'b1}), .out(O2), .sel(and_3_out));  // open: en
  Multiplexer #(.width(2)) multiplexer_3 (.in0(not_5_out), .in1({1'b1, c3[0]}), .out(O3), .sel(and_4_out));  // open: en
  Multiplexer #(.width(2)) multiplexer_4 (.in0(not_6_out), .in1(2'b11), .out(O4), .sel(and_5_out));  // open: en
  assign not_7_out = ~{32{1'b1}};  // NOT_Gate not_7, 32 bits wide
  or or_2 (Hi___LO_was_used, Op[2], Op[3], Op[4], Op[5]);
  Multiplexer #(.select(2), .width(32)) multiplexer_5 (
    .in0(_0), .in1(_1), .in2(_2), .in3(_3), .out(multiplexer_5_out), .sel(MUX));  // open: en
  assign MUX = O1 | O2 | O3 | O4;  // OR_Gate or_3, 2 bits wide
  MUX_32_32 mux_32_32_1 (
    .Selector(Op), .Data_Input_0(adder_1_out), .Data_Input_1(subtractor_1_out),
    .Data_Input_2(multiplier_1_out), .Data_Input_3(unsigned_mult_1_output), .Data_Input_4(divider_1_out),
    .Data_Input_5(unsigned_div_1_output), .Data_Input_6(adder_2_out), .Data_Input_7(And_out),
    .Data_Input_8(Or_out), .Data_Input_9(Nor_out), .Data_Input_10(Xor_out), .Data_Input_11(Andi_out),
    .Data_Input_12(Ori_out), .Data_Input_13(Xori_out), .Data_Input_14(slt_1_output),
    .Data_Input_15(unsigned_slt_1_output), .Data_Input_16(slti_1_output), .Data_Input_17(sltiu_1_output),
    .Data_Input_20(bit_extender_1_out), .Data_Input_21(not_7_out), .Data_Input_22(not_7_out),
    .Data_Input_23(not_7_out), .Data_Input_24(not_7_out), .Data_Input_25(not_7_out),
    .Data_Input_26(not_7_out), .Data_Input_27(not_7_out), .Data_Input_28(not_7_out),
    .Data_Input_29(not_7_out), .Data_Input_30(not_7_out), .Data_Input_31(not_7_out), .Output(Output));  // open: Data_Input_18, Data_Input_19
  // Probe on MUX
  Hi hi_1 (.Input(Output), .Enable(Hi___LO_was_used), .Output(Hi_Value), .Clock(Hi___LO_was_used));
  Lo lo_1 (.Input(multiplexer_5_out), .Enable(Hi___LO_was_used), .Clock(Hi___LO_was_used), .Output(Lo_Value));

  // Other names for the same wires on the sheet: a_t = Op[2]; b_t = Op[3]; c = Op[4]; d = Op[5]

  // Notes on the sheet:
  //   nop
  //   Operaciones Aritmético-Logicas
  //   Lógica de guardado para registros Hi y LO
endmodule

module Data_Path (
  input  Clock,
  input  RW,
  input  [4:0] DA,
  input  Rst,
  input  [4:0] SA,
  input  [4:0] SB,
  input  [31:0] Op,
  input  [15:0] Constant,
  input  [31:0] Pc,
  output [31:0] Data_Output,
  output [31:0] A,
  output [31:0] B,
  output [31:0] Pc_prime
);

  wire alu_2_0_1_hi___lo_was_used;
  wire [31:0] alu_2_0_1_hi_value, alu_2_0_1_lo_value;

  Register_File_x2 register_file_x2_1 (
    .Data_Input(Data_Output), .A(A), .B(B), .RW(RW), .DA(DA), .Rst(Rst), .SA(SA), .SB(SB), .Clock(Clock),
    .HI_Input(alu_2_0_1_hi_value), .LO_Input(alu_2_0_1_lo_value), .HI___LO_enable(alu_2_0_1_hi___lo_was_used));  // open: Hi_value, Lo_Value
  ALU_2_0 alu_2_0_1 (
    .A(A), .B(B), .Constant(Constant), .Op(Op), .Output(Data_Output), .Hi_Value(alu_2_0_1_hi_value),
    .Lo_Value(alu_2_0_1_lo_value), .Hi___LO_was_used(alu_2_0_1_hi___lo_was_used));
  Bc_1_0 bc_1_0_1 (.Js(Constant), .Pc(Pc), .PC_prime(Pc_prime), .Op(Op), .A(A), .B(B));
endmodule

// ID
module Instruction_Decoder (
  input  [31:0] Instruction,
  input  W_Id,
  input  Clock,
  input  Rst,
  input  [31:0] PC,
  output [31:0] Op,
  output S_Mult,
  output S_Div,
  output Mult,
  output Div,
  output [4:0] SA,
  output [4:0] SB,
  output [4:0] DA,
  output Clock_2,
  output R___W,
  output [4:0] Data_Address,
  output Reset,
  output [4:0] Sa_2,
  output [31:0] Op_2,
  output [4:0] Sb_2,
  output [15:0] Constant,
  output Jmp,
  output [31:0] PC_2
);

  wire or_3_out;
  wire [4:0] not_2_out;
  wire [15:0] not_3_out;

  Sum_Bool sum_bool_1 (.in_1({Instruction[10:0], Instruction[31:26]}), .Output(Op[0]));
  Rest_Bool rest_bool_1 (.in_1({Instruction[10:0], Instruction[31:26]}), .Output(Op[1]));
  Mult_Bool mult_bool_1 (.in_1({Instruction[31:26], Instruction[15:0]}), .Output(Op[2]));
  MULU_bool mulu_bool_1 (.in_1({Instruction[31:26], Instruction[15:0]}), .Output(Op[3]));
  DIV_bool div_bool_1 (.in_1({Instruction[31:26], Instruction[15:0]}), .Output(Op[4]));
  Unsigned_Div_Bool unsigned_div_bool_1 (.in_1({Instruction[31:26], Instruction[15:0]}), .Output(Op[5]));
  Addi_Bool addi_bool_1 (.in_1(Instruction[31:26]), .Output(Op[6]));
  And_Bool and_bool_1 (
    .in_1({Instruction[10:3], Instruction[31], Instruction[2:0], Instruction[30:26]}), .Output(Op[7]));
  Or_Bool or_bool_1 (.in_1({Instruction[10:3], Instruction[31], Instruction[2:0], Instruction[30:26]}), .Output(Op[8]));
  Nor_Bool nor_bool_1 (
    .in_1({Instruction[10:3], Instruction[31], Instruction[2:0], Instruction[30:26]}), .Output(Op[9]));
  Xor_Bool xor_bool_1 (
    .in_1({Instruction[10:3], Instruction[31], Instruction[2:0], Instruction[30:26]}), .Output(Op[10]));
  Andi_Bool andi_bool_1 (.in_1(Instruction[31:26]), .Output(Op[11]));
  Ori_Bool ori_bool_1 (.in_1(Instruction[31:26]), .Output(Op[12]));
  Xori_Bool xori_bool_1 (.in_1(Instruction[31:26]), .Output(Op[13]));
  Slt_Bool slt_bool_1 (.in_1({Instruction[31:26], Instruction[15:0]}), .Output(Op[14]));
  Unsigned_Slt_Bool unsigned_slt_bool_1 (.in_1({Instruction[31:26], Instruction[15:0]}), .Output(Op[15]));
  Slti_Bool slti_bool_1 (.in_1(Instruction[31:26]), .Output(Op[16]));
  Sltiu_Bool sltiu_bool_1 (.in_1(Instruction[31:26]), .Output(Op[17]));
  Mfhi_Bool mfhi_bool_1 (.in_1({Instruction[31:16], Instruction[10:0]}), .Output(Op[18]));
  Mflo_Bool mflo_bool_1 (.in_1({Instruction[31:16], Instruction[10:0]}), .Output(Op[19]));
  nop nop_1 (.in_1({Instruction[15:11], Instruction[31:16], Instruction[10:0]}), .Output(Op[20]));
  Beq_Bool beq_bool_1 (.in_1(Instruction[31:26]), .Output(Op[21]));
  Bne_Bool bne_bool_1 (.in_1(Instruction[31:26]), .Output(Op[22]));
  Blez_Bool blez_bool_1 (.in_1(Instruction[31:26]), .Output(Op[23]));
  Bgtz_Bool bgtz_bool_1 (.in_1(Instruction[31:26]), .Output(Op[24]));
  Bltz_Bool bltz_bool_1 (.in_1(Instruction[31:26]), .Output(Op[25]));
  Jump_Bool jump_bool_1 (.in_1(Instruction[31:26]), .Output(Op[26]));
  Jr_Bool jr_bool_1 ();  // open: in_1, Output
  or or_1 (Mult, Op[3], Op[2]);
  or or_2 (Div, Op[4], Op[5]);
  not not_1 (Op[31], 1'b1);
  or or_3 (or_3_out, Op[0], Op[1], Op[2], Op[3], Op[4], Op[5], Op[7], Op[8], Op[9], Op[10], Op[15], Op[14]);
  or or_4 (Jmp, Op[21], Op[22], Op[23], Op[24], Op[26], Op[31], Op[31], Op[25]);
  // Probe on Instruction[15:0]
  assign not_2_out = ~{5{1'b1}};  // NOT_Gate not_2, 5 bits wide
  assign not_3_out = ~{16{1'b1}};  // NOT_Gate not_3, 16 bits wide
  Multiplexer #(.width(5)) multiplexer_1 (
    .in0(Instruction[25:21]), .in1(Instruction[20:16]), .out(SA), .sel(or_3_out));  // open: en
  Multiplexer #(.width(5)) multiplexer_2 (
    .in0(not_2_out), .in1(Instruction[25:21]), .out(SB), .sel(or_3_out));  // open: en
  Multiplexer #(.width(5)) multiplexer_3 (
    .in0(Instruction[20:16]), .in1(Instruction[15:11]), .out(DA), .sel(or_3_out));  // open: en
  Multiplexer #(.width(16)) multiplexer_4 (
    .in0(Instruction[15:0]), .in1(not_3_out), .out(Constant), .sel(or_3_out));  // open: en
  // Probe on {{5{Op[31]}}, Op[26:0]}

  assign Clock_2 = Clock;
  assign Data_Address = DA;
  assign Op[30:27] = {4{Op[31]}};
  assign Op_2 = {{5{Op[31]}}, Op[26:0]};
  assign PC_2 = PC;
  assign R___W = W_Id;
  assign Reset = Rst;
  assign S_Div = Div;
  assign S_Mult = Mult;
  assign Sa_2 = SA;
  assign Sb_2 = SB;
endmodule

// Bc
module Bc_1_0 (
  input  [31:0] A,
  input  [31:0] B,
  input  [15:0] Js,
  input  [31:0] Op,
  input  [31:0] Pc,
  output [31:0] PC_prime
);

  wire [31:0] beq_1_pc_prime, not_1_out;

  assign not_1_out = ~{32{1'b1}};  // NOT_Gate not_1, 32 bits wide
  Beq beq_1 (.A(A), .B(B), .PC(Pc), .Js(Js), .PC_prime(beq_1_pc_prime));
  MUX_32_32 mux_32_32_1 (
    .Selector(Op), .Data_Input_0(not_1_out), .Data_Input_1(not_1_out), .Data_Input_2(not_1_out),
    .Data_Input_3(not_1_out), .Data_Input_4(not_1_out), .Data_Input_5(not_1_out), .Data_Input_6(not_1_out),
    .Data_Input_7(not_1_out), .Data_Input_8(not_1_out), .Data_Input_9(not_1_out), .Data_Input_10(not_1_out),
    .Data_Input_11(not_1_out), .Data_Input_12(not_1_out), .Data_Input_13(not_1_out),
    .Data_Input_14(not_1_out), .Data_Input_15(not_1_out), .Data_Input_16(not_1_out),
    .Data_Input_17(not_1_out), .Data_Input_18(not_1_out), .Data_Input_19(not_1_out),
    .Data_Input_20(not_1_out), .Data_Input_21(beq_1_pc_prime), .Output(PC_prime));  // open: Data_Input_22, Data_Input_23, Data_Input_24, Data_Input_25, Data_Input_26, Data_Input_27, Data_Input_28, Data_Input_29, Data_Input_30, Data_Input_31
endmodule

// C2
module PC_2_0 (
  input  [31:0] Input,
  output [31:0] Sum
);

  wire [2:2] not_2_out;
  wire [15:0] not_1_out;
  wire [31:0] bit_extender_1_out;

  assign not_1_out = ~{16{1'b1}};  // NOT_Gate not_1, 16 bits wide
  not not_2 (not_2_out[2], not_1_out[2]);
  assign bit_extender_1_out = {{16{1'b0}}, {not_1_out[15:3], not_2_out[2], not_1_out[1:0]}};  // Bit_Extender bit_extender_1
  Adder #(.width(32)) adder_1 (.a(Input), .b(bit_extender_1_out), .out(Sum));  // open: cin, cout

  // Notes on the sheet:
  //   Sumador del PC por defecto (sumar 4)
endmodule

// PC
module PC_3_0 (
  input  Clock_1,
  input  Clock_2,
  input  Rst,
  input  [31:0] ADDR,
  input  [31:0] PC_prime_input,
  input  Jmp,
  output [31:0] PC,
  output [31:0] PC_prime
);

  wire counter_1_q;
  wire [31:0] multiplexer_1_out, multiplexer_2_out, pc_2_0_1_sum;

  Counter #(.width(1), .max('h1), .ongoal("stay")) counter_1 (
    .Q(counter_1_q), .clk(Clock_1), .clr(Rst));  // open: load, D, count, carry
  Multiplexer #(.width(32)) multiplexer_1 (
    .in0(ADDR), .in1(PC_prime), .out(multiplexer_1_out), .sel(counter_1_q));  // open: en
  // Probe on PC
  Register #(.width(32)) Dir_1 (.D(multiplexer_1_out), .Q(PC), .clk(Clock_1), .clr(Rst));  // open: en
  PC_2_0 pc_2_0_1 (.Input(PC), .Sum(pc_2_0_1_sum));
  Multiplexer #(.width(32)) multiplexer_2 (
    .in0(pc_2_0_1_sum), .in1(PC_prime_input), .out(multiplexer_2_out), .sel(Jmp));  // open: en
  Register #(.width(32)) Dir_2 (.D(multiplexer_2_out), .Q(PC_prime), .clk(Clock_2), .clr(Rst));  // open: en

  // Notes on the sheet:
  //   Program Counter 
endmodule

// HI
module Hi (
  input  [31:0] Input,
  input  Enable,
  input  Clock,
  output [31:0] Output
);

  Register #(.width(32)) register_1 (.D(Input), .en(Enable), .Q(Output), .clk(Clock));  // open: clr
endmodule

// LO
module Lo (
  input  [31:0] Input,
  input  Enable,
  input  Clock,
  output [31:0] Output
);

  Register #(.width(32)) register_1 (.D(Input), .en(Enable), .Q(Output), .clk(Clock));  // open: clr
endmodule

// +
module Sum_Bool (
  input  [16:0] in_1,
  output Output
);

  wire not_1_out, not_2_out, not_3_out, not_4_out, not_5_out, not_6_out, not_7_out, not_8_out, not_9_out,
       not_10_out, not_11_out, not_12_out, not_13_out, not_14_out, not_15_out, not_16_out;

  not not_1 (not_1_out, in_1[0]);
  not not_2 (not_2_out, in_1[1]);
  not not_3 (not_3_out, in_1[2]);
  not not_4 (not_4_out, in_1[3]);
  not not_5 (not_5_out, in_1[4]);
  not not_6 (not_6_out, in_1[5]);
  not not_7 (not_7_out, in_1[6]);
  not not_8 (not_8_out, in_1[7]);
  and and_1 (Output, not_1_out, not_2_out, not_3_out, not_4_out, not_5_out, not_6_out, not_7_out, not_8_out, not_9_out, not_10_out, not_11_out, in_1[11], not_12_out, not_13_out, not_14_out, not_15_out, not_16_out);
  not not_9 (not_9_out, in_1[8]);
  not not_10 (not_10_out, in_1[9]);
  not not_11 (not_11_out, in_1[10]);
  not not_12 (not_12_out, in_1[12]);
  not not_13 (not_13_out, in_1[13]);
  not not_14 (not_14_out, in_1[14]);
  not not_15 (not_15_out, in_1[15]);
  not not_16 (not_16_out, in_1[16]);
endmodule

// -
module Rest_Bool (
  input  [16:0] in_1,
  output Output
);

  and and_1 (Output, ~in_1[0], ~in_1[1], ~in_1[2], ~in_1[3], ~in_1[4], ~in_1[5], ~in_1[6], in_1[7], ~in_1[8], ~in_1[9], ~in_1[10], in_1[11], ~in_1[12], ~in_1[13], ~in_1[14], ~in_1[15], ~in_1[16]);  // AND_Gate
endmodule

// *
module Mult_Bool (
  input  [21:0] in_1,
  output Output
);

  wire not_1_out, not_2_out, or_1_out, or_2_out;

  or or_1 (or_1_out, in_1[0], in_1[1], in_1[2], ~in_1[3], ~in_1[4], in_1[5]);  // OR_Gate
  not not_1 (not_1_out, or_1_out);
  not not_2 (not_2_out, or_2_out);
  or or_2 (or_2_out, in_1[6], in_1[7], in_1[8], in_1[9], in_1[10], in_1[11], in_1[12], in_1[13], in_1[14], in_1[15], in_1[16], in_1[17], in_1[18], in_1[19], in_1[20], in_1[21]);
  and and_1 (Output, not_1_out, not_2_out);
endmodule

// **
module MULU_bool (
  input  [21:0] in_1,
  output Output
);

  wire not_1_out, not_2_out, or_1_out, or_2_out;

  not not_1 (not_1_out, or_1_out);
  or or_1 (or_1_out, ~in_1[0], in_1[1], in_1[2], ~in_1[3], ~in_1[4], in_1[5]);  // OR_Gate
  or or_2 (or_2_out, in_1[6], in_1[7], in_1[8], in_1[9], in_1[10], in_1[11], in_1[12], in_1[13], in_1[14], in_1[15], in_1[16], in_1[17], in_1[18], in_1[19], in_1[20], in_1[21]);
  not not_2 (not_2_out, or_2_out);
  and and_1 (Output, not_1_out, not_2_out);
endmodule

// /
module DIV_bool (
  input  [21:0] in_1,
  output Output
);

  wire not_1_out, not_2_out, or_1_out, or_2_out;

  not not_1 (not_1_out, or_1_out);
  or or_1 (or_1_out, in_1[0], ~in_1[1], in_1[2], ~in_1[3], ~in_1[4], in_1[5]);  // OR_Gate
  not not_2 (not_2_out, or_2_out);
  or or_2 (or_2_out, in_1[6], in_1[7], in_1[8], in_1[9], in_1[10], in_1[11], in_1[12], in_1[13], in_1[14], in_1[15], in_1[16], in_1[17], in_1[18], in_1[19], in_1[20], in_1[21]);
  and and_1 (Output, not_1_out, not_2_out);
endmodule

// //
module Unsigned_Div_Bool (
  input  [21:0] in_1,
  output Output
);

  wire not_1_out, not_2_out, or_1_out, or_2_out;

  not not_1 (not_1_out, or_1_out);
  or or_1 (or_1_out, ~in_1[0], ~in_1[1], in_1[2], ~in_1[3], ~in_1[4], in_1[5]);  // OR_Gate
  not not_2 (not_2_out, or_2_out);
  or or_2 (or_2_out, in_1[6], in_1[7], in_1[8], in_1[9], in_1[10], in_1[11], in_1[12], in_1[13], in_1[14], in_1[15], in_1[16], in_1[17], in_1[18], in_1[19], in_1[20], in_1[21]);
  and and_1 (Output, not_1_out, not_2_out);
endmodule

// ++
module Addi_Bool (
  input  [5:0] in_1,
  output Output
);

  wire or_1_out;

  not not_1 (Output, or_1_out);
  or or_1 (or_1_out, in_1[0], in_1[1], in_1[2], ~in_1[3], in_1[4], in_1[5]);  // OR_Gate
endmodule

// And
module And_Bool (
  input  [16:0] in_1,
  output Output
);

  wire or_1_out;

  or or_1 (or_1_out, in_1[0], in_1[1], in_1[2], in_1[3], in_1[4], in_1[5], in_1[6], ~in_1[7], in_1[8], in_1[9], in_1[10], ~in_1[11], in_1[12], in_1[13], in_1[14], in_1[15], in_1[16]);  // OR_Gate
  not not_1 (Output, or_1_out);
endmodule

// Or
module Or_Bool (
  input  [16:0] in_1,
  output Output
);

  wire or_1_out;

  or or_1 (or_1_out, in_1[0], in_1[1], in_1[2], in_1[3], in_1[4], ~in_1[5], in_1[6], ~in_1[7], in_1[8], in_1[9], in_1[10], ~in_1[11], in_1[12], in_1[13], in_1[14], in_1[15], in_1[16]);  // OR_Gate
  not not_1 (Output, or_1_out);
endmodule

// Nor
module Nor_Bool (
  input  [16:0] in_1,
  output Output
);

  wire or_1_out;

  or or_1 (or_1_out, in_1[0], in_1[1], in_1[2], in_1[3], in_1[4], ~in_1[5], ~in_1[6], ~in_1[7], in_1[8], in_1[9], in_1[10], ~in_1[11], in_1[12], in_1[13], in_1[14], in_1[15], in_1[16]);  // OR_Gate
  not not_1 (Output, or_1_out);
endmodule

// Xor
module Xor_Bool (
  input  [16:0] in_1,
  output Output
);

  wire or_1_out;

  not not_1 (Output, or_1_out);
  or or_1 (or_1_out, in_1[0], in_1[1], in_1[2], in_1[3], in_1[4], in_1[5], in_1[6], in_1[7], in_1[8], ~in_1[9], in_1[10], ~in_1[11], in_1[12], in_1[13], in_1[14], in_1[15], in_1[16]);  // OR_Gate
endmodule

// Andi
module Andi_Bool (
  input  [5:0] in_1,
  output Output
);

  wire or_1_out;

  or or_1 (or_1_out, in_1[0], in_1[1], ~in_1[2], ~in_1[3], in_1[4], in_1[5]);  // OR_Gate
  not not_1 (Output, or_1_out);
endmodule

// Ori
module Ori_Bool (
  input  [5:0] in_1,
  output Output
);

  wire or_1_out;

  or or_1 (or_1_out, ~in_1[0], in_1[1], ~in_1[2], ~in_1[3], in_1[4], in_1[5]);  // OR_Gate
  not not_1 (Output, or_1_out);
endmodule

// Xori
module Xori_Bool (
  input  [5:0] in_1,
  output Output
);

  wire or_1_out;

  or or_1 (or_1_out, in_1[0], ~in_1[1], ~in_1[2], ~in_1[3], in_1[4], in_1[5]);  // OR_Gate
  not not_1 (Output, or_1_out);
endmodule

// Slt
module Slt_Bool (
  input  [21:0] in_1,
  output Output
);

  wire or_1_out;

  or or_1 (or_1_out, in_1[0], ~in_1[1], in_1[2], ~in_1[3], in_1[4], ~in_1[5], in_1[6], in_1[7], in_1[8], in_1[9], in_1[10], in_1[12], in_1[13], in_1[14], in_1[15], in_1[16], in_1[17], in_1[18], in_1[19], in_1[20], in_1[21], in_1[11]);  // OR_Gate
  not not_1 (Output, or_1_out);
endmodule

// U/Slt
module Unsigned_Slt_Bool (
  input  [21:0] in_1,
  output Output
);

  wire or_1_out;

  or or_1 (or_1_out, ~in_1[0], ~in_1[1], in_1[2], ~in_1[3], in_1[4], ~in_1[5], in_1[6], in_1[7], in_1[8], in_1[9], in_1[10], in_1[12], in_1[13], in_1[14], in_1[15], in_1[16], in_1[17], in_1[18], in_1[19], in_1[20], in_1[21], in_1[11]);  // OR_Gate
  not not_1 (Output, or_1_out);
endmodule

// Slti
module Slti_Bool (
  input  [5:0] in_1,
  output Output
);

  wire or_1_out;

  or or_1 (or_1_out, in_1[0], ~in_1[1], in_1[2], in_1[4], in_1[5], ~in_1[3]);  // OR_Gate
  not not_1 (Output, or_1_out);
endmodule

// Sltiu
module Sltiu_Bool (
  input  [5:0] in_1,
  output Output
);

  wire or_1_out;

  or or_1 (or_1_out, ~in_1[0], ~in_1[1], in_1[2], in_1[4], in_1[5], ~in_1[3]);  // OR_Gate
  not not_1 (Output, or_1_out);
endmodule

// Mfhi
module Mfhi_Bool (
  input  [26:0] in_1,
  output Output
);

  wire or_1_out;

  or or_1 (or_1_out, in_1[0], in_1[1], in_1[2], in_1[3], ~in_1[4], in_1[5], in_1[6], in_1[7], in_1[8], in_1[9], in_1[10], in_1[11], in_1[12], in_1[13], in_1[14], in_1[15], in_1[16], in_1[17], in_1[18], in_1[19], in_1[20], in_1[21], in_1[22], in_1[23], in_1[24], in_1[25], in_1[26]);  // OR_Gate
  not not_1 (Output, or_1_out);
endmodule

// Mflo
module Mflo_Bool (
  input  [26:0] in_1,
  output Output
);

  wire or_1_out;

  or or_1 (or_1_out, in_1[0], ~in_1[1], in_1[2], in_1[3], ~in_1[4], in_1[5], in_1[6], in_1[7], in_1[8], in_1[9], in_1[10], in_1[11], in_1[12], in_1[13], in_1[14], in_1[15], in_1[16], in_1[17], in_1[18], in_1[19], in_1[20], in_1[21], in_1[22], in_1[23], in_1[24], in_1[25], in_1[26]);  // OR_Gate
  not not_1 (Output, or_1_out);
endmodule

// Beq
module Beq_Bool (
  input  [5:0] in_1,
  output Output
);

  wire or_1_out;

  or or_1 (or_1_out, in_1[0], in_1[1], ~in_1[2], in_1[4], in_1[5], in_1[3]);  // OR_Gate
  not not_1 (Output, or_1_out);
endmodule

// Bne
module Bne_bool (
  input  [5:0] in_1,
  output Output
);

  wire or_1_out;

  or or_1 (or_1_out, ~in_1[0], in_1[1], ~in_1[2], in_1[4], in_1[5], in_1[3]);  // OR_Gate
  not not_1 (Output, or_1_out);
endmodule

// Bne
module Bne_Bool (
  input  [5:0] in_1,
  output Output
);

  wire or_1_out;

  or or_1 (or_1_out, ~in_1[0], in_1[1], ~in_1[2], in_1[4], in_1[5], in_1[3]);  // OR_Gate
  not not_1 (Output, or_1_out);
endmodule

// Blez
module Blez_Bool (
  input  [5:0] in_1,
  output Output
);

  wire or_1_out;

  or or_1 (or_1_out, in_1[0], ~in_1[1], ~in_1[2], in_1[4], in_1[5], in_1[3]);  // OR_Gate
  not not_1 (Output, or_1_out);
endmodule

// Bgtz
module Bgtz_Bool (
  input  [5:0] in_1,
  output Output
);

  wire or_1_out;

  or or_1 (or_1_out, ~in_1[0], ~in_1[1], ~in_1[2], in_1[4], in_1[5], in_1[3]);  // OR_Gate
  not not_1 (Output, or_1_out);
endmodule

// Bltz
module Bltz_Bool (
  input  [5:0] in_1,
  output Output
);

  wire or_1_out;

  or or_1 (or_1_out, ~in_1[0], in_1[1], in_1[2], in_1[4], in_1[5], in_1[3]);  // OR_Gate
  not not_1 (Output, or_1_out);
endmodule

// Jump
module Jump_Bool (
  input  [5:0] in_1,
  output Output
);

  wire or_1_out;

  or or_1 (or_1_out, in_1[0], ~in_1[1], in_1[2], in_1[4], in_1[5], in_1[3]);  // OR_Gate
  not not_1 (Output, or_1_out);
endmodule

// Jr
module Jr_Bool (
  input  [26:0] in_1,
  output Output
);

  wire or_1_out;

  or or_1 (or_1_out, in_1[0], in_1[1], in_1[2], ~in_1[3], in_1[4], in_1[5], in_1[6], in_1[7], in_1[8], in_1[9], in_1[10], in_1[11], in_1[12], in_1[13], in_1[14], in_1[15], in_1[16], in_1[17], in_1[18], in_1[19], in_1[20], in_1[21], in_1[22], in_1[23], in_1[24], in_1[25], in_1[26]);  // OR_Gate
  not not_1 (Output, or_1_out);
endmodule

// Mult
module Unsigned_Mult (
  input  [31:0] in_1,
  input  [31:0] in_2,
  output [31:0] Output,
  output [31:0] Output_2
);

  wire [31:0] complemento_a_2_1_output, complemento_a_2_2_output, multiplexer_1_out, multiplexer_2_out;

  Complemento_a_2 complemento_a_2_1 (.Input(in_1), .Output(complemento_a_2_1_output));
  Complemento_a_2 complemento_a_2_2 (.Input(in_2), .Output(complemento_a_2_2_output));
  Multiplexer #(.width(32)) multiplexer_1 (
    .in0(in_1), .in1(complemento_a_2_1_output), .out(multiplexer_1_out), .sel(in_1[31]));  // open: en
  Multiplexer #(.width(32)) multiplexer_2 (
    .in0(in_2), .in1(complemento_a_2_2_output), .out(multiplexer_2_out), .sel(in_2[31]));  // open: en
  Multiplier #(.width(32)) multiplier_1 (
    .a(multiplexer_1_out), .b(multiplexer_2_out), .out(Output), .cout(Output_2));  // open: cin
endmodule

// Div
module Unsigned_Div (
  input  [31:0] in_1,
  input  [31:0] in_2,
  output [31:0] Output,
  output [31:0] Output_2
);

  wire [31:0] complemento_a_2_1_output, complemento_a_2_2_output, multiplexer_1_out, multiplexer_2_out;

  Complemento_a_2 complemento_a_2_1 (.Input(in_1), .Output(complemento_a_2_1_output));
  Complemento_a_2 complemento_a_2_2 (.Input(in_2), .Output(complemento_a_2_2_output));
  Multiplexer #(.width(32)) multiplexer_1 (
    .in0(in_1), .in1(complemento_a_2_1_output), .out(multiplexer_1_out), .sel(in_1[31]));  // open: en
  Multiplexer #(.width(32)) multiplexer_2 (
    .in0(in_2), .in1(complemento_a_2_2_output), .out(multiplexer_2_out), .sel(in_2[31]));  // open: en
  Divider #(.width(32)) divider_1 (
    .a(multiplexer_1_out), .b(multiplexer_2_out), .out(Output), .rem(Output_2));  // open: upper
endmodule

module Slt (
  input  [31:0] Rs,
  input  [31:0] Rt,
  output [31:0] Output
);

  wire comparator_1_lt;
  wire [0:0] not_16_out;
  wire [15:0] multiplexer_1_out;
  wire [15:1] not_1_out;

  not not_1 (not_1_out[1], 1'b1);
  not not_2 (not_1_out[2], 1'b1);
  not not_3 (not_1_out[3], 1'b1);
  not not_4 (not_1_out[4], 1'b1);
  not not_5 (not_1_out[5], 1'b1);
  not not_6 (not_1_out[6], 1'b1);
  not not_7 (not_1_out[7], 1'b1);
  not not_8 (not_1_out[8], 1'b1);
  not not_9 (not_1_out[9], 1'b1);
  not not_10 (not_1_out[10], 1'b1);
  not not_11 (not_1_out[11], 1'b1);
  not not_12 (not_1_out[12], 1'b1);
  not not_13 (not_1_out[13], 1'b1);
  not not_14 (not_1_out[14], 1'b1);
  not not_15 (not_1_out[15], 1'b1);
  Comparator #(.width(32)) comparator_1 (.a(Rs), .b(Rt), .lt(comparator_1_lt));  // open: gt, eq
  not not_16 (not_16_out[0], 1'b1);
  Multiplexer #(.width(16)) multiplexer_1 (
    .in0({not_1_out, not_16_out[0]}), .in1({not_1_out, 1'b1}), .out(multiplexer_1_out), .sel(comparator_1_lt));  // open: en
  assign Output = {{16{1'b0}}, multiplexer_1_out};  // Bit_Extender bit_extender_1
endmodule

module Slti (
  input  [31:0] Rs,
  input  [31:0] Constant,
  output [31:0] Output
);

  wire comparator_1_lt;
  wire [0:0] not_16_out;
  wire [15:0] multiplexer_1_out;
  wire [15:1] not_1_out;

  not not_1 (not_1_out[1], 1'b1);
  not not_2 (not_1_out[2], 1'b1);
  not not_3 (not_1_out[3], 1'b1);
  not not_4 (not_1_out[4], 1'b1);
  not not_5 (not_1_out[5], 1'b1);
  not not_6 (not_1_out[6], 1'b1);
  not not_7 (not_1_out[7], 1'b1);
  not not_8 (not_1_out[8], 1'b1);
  not not_9 (not_1_out[9], 1'b1);
  not not_10 (not_1_out[10], 1'b1);
  not not_11 (not_1_out[11], 1'b1);
  not not_12 (not_1_out[12], 1'b1);
  not not_13 (not_1_out[13], 1'b1);
  not not_14 (not_1_out[14], 1'b1);
  not not_15 (not_1_out[15], 1'b1);
  Comparator #(.width(32)) comparator_1 (.a(Rs), .b(Constant), .lt(comparator_1_lt));  // open: gt, eq
  not not_16 (not_16_out[0], 1'b1);
  Multiplexer #(.width(16)) multiplexer_1 (
    .in0({not_1_out, not_16_out[0]}), .in1({not_1_out, 1'b1}), .out(multiplexer_1_out), .sel(comparator_1_lt));  // open: en
  assign Output = {{16{1'b0}}, multiplexer_1_out};  // Bit_Extender bit_extender_1
endmodule

module Sltiu (
  input  [31:0] Rs,
  input  [31:0] Constant,
  output [31:0] Output
);

  wire comparator_1_lt;
  wire [0:0] not_16_out;
  wire [15:0] multiplexer_1_out;
  wire [15:1] not_1_out;

  not not_1 (not_1_out[1], 1'b1);
  not not_2 (not_1_out[2], 1'b1);
  not not_3 (not_1_out[3], 1'b1);
  not not_4 (not_1_out[4], 1'b1);
  not not_5 (not_1_out[5], 1'b1);
  not not_6 (not_1_out[6], 1'b1);
  not not_7 (not_1_out[7], 1'b1);
  not not_8 (not_1_out[8], 1'b1);
  not not_9 (not_1_out[9], 1'b1);
  not not_10 (not_1_out[10], 1'b1);
  not not_11 (not_1_out[11], 1'b1);
  not not_12 (not_1_out[12], 1'b1);
  not not_13 (not_1_out[13], 1'b1);
  not not_14 (not_1_out[14], 1'b1);
  not not_15 (not_1_out[15], 1'b1);
  Comparator #(.width(32)) comparator_1 (.a(Rs), .b(Constant), .lt(comparator_1_lt));  // open: gt, eq
  not not_16 (not_16_out[0], 1'b1);
  Multiplexer #(.width(16)) multiplexer_1 (
    .in0({not_1_out, not_16_out[0]}), .in1({not_1_out, 1'b1}), .out(multiplexer_1_out), .sel(comparator_1_lt));  // open: en
  assign Output = {{16{1'b0}}, multiplexer_1_out};  // Bit_Extender bit_extender_1
endmodule

// U / Slt
module Unsigned_Slt (
  input  [31:0] Rs,
  input  [31:0] Rt,
  output [31:0] Output
);

  wire comparator_1_lt;
  wire [0:0] not_16_out;
  wire [15:0] multiplexer_1_out;
  wire [15:1] not_1_out;

  not not_1 (not_1_out[1], 1'b1);
  not not_2 (not_1_out[2], 1'b1);
  not not_3 (not_1_out[3], 1'b1);
  not not_4 (not_1_out[4], 1'b1);
  not not_5 (not_1_out[5], 1'b1);
  not not_6 (not_1_out[6], 1'b1);
  not not_7 (not_1_out[7], 1'b1);
  not not_8 (not_1_out[8], 1'b1);
  not not_9 (not_1_out[9], 1'b1);
  not not_10 (not_1_out[10], 1'b1);
  not not_11 (not_1_out[11], 1'b1);
  not not_12 (not_1_out[12], 1'b1);
  not not_13 (not_1_out[13], 1'b1);
  not not_14 (not_1_out[14], 1'b1);
  not not_15 (not_1_out[15], 1'b1);
  Comparator #(.width(32), .mode("unsigned")) comparator_1 (.a(Rs), .b(Rt), .lt(comparator_1_lt));  // open: gt, eq
  not not_16 (not_16_out[0], 1'b1);
  Multiplexer #(.width(16)) multiplexer_1 (
    .in0({not_1_out, not_16_out[0]}), .in1({not_1_out, 1'b1}), .out(multiplexer_1_out), .sel(comparator_1_lt));  // open: en
  assign Output = {{16{1'b0}}, multiplexer_1_out};  // Bit_Extender bit_extender_1
endmodule

module Complemento_a_2 (
  input  [31:0] Input,
  output [31:0] Output
);

  wire [31:0] bit_extender_1_out, not_1_out;

  assign not_1_out = ~Input;  // NOT_Gate not_1, 32 bits wide
  assign bit_extender_1_out = {{31{1'b0}}, 1'b1};  // Bit_Extender bit_extender_1
  // Probe on bit_extender_1_out
  Adder #(.width(32)) adder_1 (.a(not_1_out), .b(bit_extender_1_out), .out(Output));  // open: cin, cout
endmodule

// Nop
module nop (
  input  [31:0] in_1,
  output Output
);

  wire or_1_out;

  or or_1 (or_1_out, in_1[0], in_1[1], in_1[2], in_1[3], in_1[4], in_1[5], in_1[6], in_1[7], in_1[8], in_1[9], in_1[10], in_1[11], in_1[12], in_1[13], in_1[14], in_1[15], in_1[17], in_1[18], in_1[19], in_1[20], in_1[21], in_1[22], in_1[23], in_1[24], in_1[25], in_1[26], in_1[27], in_1[28], in_1[29], in_1[30], in_1[31], in_1[16]);
  not not_1 (Output, or_1_out);
endmodule

module Beq (
  input  [31:0] A,
  input  [31:0] B,
  input  [31:0] PC,
  input  [15:0] Js,
  output [31:0] PC_prime
);

  wire comparator_1_eq;
  wire [2:2] not_1_out;
  wire [31:0] _4, adder_1_out, bit_extender_1_out, S1, S2;

  assign {_4[31:3], not_1_out[2], _4[1:0]} = ~{32{1'b1}};  // NOT_Gate not_1, 32 bits wide
  assign bit_extender_1_out = {{16{1'b0}}, Js};  // Bit_Extender bit_extender_1
  not not_2 (_4[2], not_1_out[2]);
  Comparator #(.width(32)) comparator_1 (.a(A), .b(B), .eq(comparator_1_eq));  // open: gt, lt
  Adder #(.width(32)) adder_1 (.a(PC), .b(bit_extender_1_out), .out(adder_1_out));  // open: cin, cout
  Multiplexer #(.width(32)) multiplexer_1 (.in0(S1), .in1(S2), .out(PC_prime), .sel(comparator_1_eq));  // open: en
  Adder #(.width(32)) adder_2 (.a(PC), .b(_4), .out(S1));  // open: cin, cout
  Adder #(.width(32)) adder_3 (.a(adder_1_out), .b(_4), .out(S2));  // open: cin, cout
endmodule

module Bne (
  input  [15:0] A,
  input  [15:0] B,
  input  [15:0] PC,
  input  [15:0] Js,
  output [15:0] PC_prime
);

  wire comparator_1_eq;
  wire [2:2] not_1_out;
  wire [15:0] _4, adder_1_out, S1, S2;

  assign {_4[15:3], not_1_out[2], _4[1:0]} = ~{16{1'b1}};  // NOT_Gate not_1, 16 bits wide
  not not_2 (_4[2], not_1_out[2]);
  Comparator #(.width(16)) comparator_1 (.a(A), .b(B), .eq(comparator_1_eq));  // open: gt, lt
  Adder #(.width(16)) adder_1 (.a(PC), .b(Js), .out(adder_1_out));  // open: cin, cout
  Multiplexer #(.width(16)) multiplexer_1 (.in0(S1), .in1(S2), .out(PC_prime), .sel(comparator_1_eq));  // open: en
  Adder #(.width(16)) adder_2 (.a(PC), .b(_4), .out(S2));  // open: cin, cout
  Adder #(.width(16)) adder_3 (.a(adder_1_out), .b(_4), .out(S1));  // open: cin, cout
endmodule

module Blez (
  input  [15:0] A,
  input  [15:0] PC,
  input  [15:0] Js,
  output [15:0] PC_prime
);

  wire comparator_1_eq, comparator_1_lt, or_1_out;
  wire [2:2] not_1_out;
  wire [15:0] _0, _4, adder_1_out, S1, S2;

  assign {_4[15:3], not_1_out[2], _4[1:0]} = ~{16{1'b1}};  // NOT_Gate not_1, 16 bits wide
  assign _0 = ~{16{1'b1}};  // NOT_Gate not_2, 16 bits wide
  not not_3 (_4[2], not_1_out[2]);
  Comparator #(.width(16)) comparator_1 (.a(A), .b(_0), .eq(comparator_1_eq), .lt(comparator_1_lt));  // open: gt
  Adder #(.width(16)) adder_1 (.a(PC), .b(Js), .out(adder_1_out));  // open: cin, cout
  Multiplexer #(.width(16)) multiplexer_1 (.in0(S1), .in1(S2), .out(PC_prime), .sel(or_1_out));  // open: en
  or or_1 (or_1_out, comparator_1_eq, comparator_1_lt);
  Adder #(.width(16)) adder_2 (.a(PC), .b(_4), .out(S1));  // open: cin, cout
  Adder #(.width(16)) adder_3 (.a(adder_1_out), .b(_4), .out(S2));  // open: cin, cout
endmodule

module Bgtz (
  input  [15:0] A,
  input  [15:0] PC,
  input  [15:0] Js,
  output [15:0] PC_prime
);

  wire comparator_1_eq, comparator_1_lt, or_1_out;
  wire [2:2] not_1_out;
  wire [15:0] _0, _4, adder_1_out, S1, S2;

  assign {_4[15:3], not_1_out[2], _4[1:0]} = ~{16{1'b1}};  // NOT_Gate not_1, 16 bits wide
  assign _0 = ~{16{1'b1}};  // NOT_Gate not_2, 16 bits wide
  not not_3 (_4[2], not_1_out[2]);
  Comparator #(.width(16)) comparator_1 (.a(A), .b(_0), .eq(comparator_1_eq), .lt(comparator_1_lt));  // open: gt
  Adder #(.width(16)) adder_1 (.a(PC), .b(Js), .out(adder_1_out));  // open: cin, cout
  Multiplexer #(.width(16)) multiplexer_1 (.in0(S1), .in1(S2), .out(PC_prime), .sel(or_1_out));  // open: en
  or or_1 (or_1_out, comparator_1_eq, comparator_1_lt);
  Adder #(.width(16)) adder_2 (.a(PC), .b(_4), .out(S2));  // open: cin, cout
  Adder #(.width(16)) adder_3 (.a(adder_1_out), .b(_4), .out(S1));  // open: cin, cout
endmodule

module Bltz (
  input  [15:0] A,
  input  [15:0] PC,
  input  [15:0] Js,
  output [15:0] PC_prime
);

  wire comparator_1_lt;
  wire [2:2] not_1_out;
  wire [15:0] _0, _4, adder_1_out, S1, S2;

  assign {_4[15:3], not_1_out[2], _4[1:0]} = ~{16{1'b1}};  // NOT_Gate not_1, 16 bits wide
  assign _0 = ~{16{1'b1}};  // NOT_Gate not_2, 16 bits wide
  not not_3 (_4[2], not_1_out[2]);
  Comparator #(.width(16)) comparator_1 (.a(A), .b(_0), .lt(comparator_1_lt));  // open: gt, eq
  Adder #(.width(16)) adder_1 (.a(PC), .b(Js), .out(adder_1_out));  // open: cin, cout
  Multiplexer #(.width(16)) multiplexer_1 (.in0(S1), .in1(S2), .out(PC_prime), .sel(comparator_1_lt));  // open: en
  Adder #(.width(16)) adder_2 (.a(PC), .b(_4), .out(S1));  // open: cin, cout
  Adder #(.width(16)) adder_3 (.a(adder_1_out), .b(_4), .out(S2));  // open: cin, cout
endmodule

module Jr (
  input  [15:0] A,
  output [15:0] PC_prime
);


  assign PC_prime = A;
endmodule
